// Logisim project 16BitCPU.circ as structural Verilog: 14 circuits, main circuit main
module CLOCK (
  input  HALT,
  input  CLK_SWITCH,
  input  CLK_STEP,
  output CLK
);

  wire and_1_out, and_2_out, clock_1_out, not_1_out, not_2_out, or_1_out;

  Clock clock_1 (.out(clock_1_out));
  Pull_Resistor pull_resistor_1 (.node(CLK_SWITCH));
  Pull_Resistor pull_resistor_2 (.node(CLK_STEP));
  and and_1 (and_1_out, clock_1_out, not_1_out);
  not not_1 (not_1_out, CLK_SWITCH);
  and and_2 (and_2_out, CLK_SWITCH, CLK_STEP);
  not not_2 (not_2_out, HALT);
  or or_1 (or_1_out, and_1_out, and_2_out);
  and and_3 (CLK, not_2_out, or_1_out);
endmodule

module main (
);

  wire A_IN, A_OUT, A_RST, and_1_out, B_IN, B_OUT, B_RST, buffer_1_out, buffer_27_out, buffer_28_out,
       buffer_29_out, buffer_30_out, buffer_31_out, buffer_32_out, buffer_33_out, button_1_out, button_2_out,
       CF, CLC_RST, dipswitch_1_p1, dipswitch_2_p1, dipswitch_3_p1, E_OUT, F_IN, F_RST, HALT, I_IN, I_OUT,
       I_RST, J, M_IN, M_OUT, MA_IN, MA_RST, O_IN, O_RST, or_1_out, output_7segment_1_neg, PC_OUT, PCE,
       program_rom_1_done, SU, switch_1_p2, switch_2_p2, TWOS, ZF;
  wire [3:0] control_logic_1_step;
  wire [7:0] register_1_a_bus, register_1_a_bus_2;
  wire [15:0] alu_1_leds, gen_register_1_a_bus, gen_register_1_leds, gen_register_2_a_bus,
       gen_register_2_leds, plex_16_1_b16_3, program_counter_1_leds, program_rom_1_addr, program_rom_1_data,
       ram_addr_register_1_ram_bus, register_1_leds;
  wire [17:0] plex_18_1_b18_3, ram_1_bus_2;
  wire [17:16] undriven;
  wire [31:0] control_logic_1_clo, output_7segment_1__7segment;

  Button button_1 (.out(button_1_out));
  DotMatrix #(.inputtype("row"), .matrixcols(16), .matrixrows(1)) dotmatrix_1 (.row0(program_rom_1_addr));
  DotMatrix #(.inputtype("row"), .matrixcols(16), .matrixrows(1)) dotmatrix_2 (.row0(program_rom_1_data));
  // DipSwitch #(.NSwitches(1)) dipswitch_1: pin names not known; wires that end beside it: dipswitch_1_p1
  and and_1 (and_1_out, dipswitch_1_p1, button_1_out);
  // DipSwitch #(.NSwitches(1)) dipswitch_2: pin names not known; wires that end beside it: dipswitch_2_p1
  LED led_1 (.in(program_rom_1_done));
  PROGRAM_ROM program_rom_1 (
    .ENB(dipswitch_1_p1), .R_CLK(and_1_out), .R_RST(dipswitch_2_p1), .DONE(program_rom_1_done),
    .ADDR(program_rom_1_addr), .DATA(program_rom_1_data));
  DotMatrix #(.inputtype("row"), .matrixcols(32), .matrixrows(1)) dotmatrix_3 (.row0(control_logic_1_clo));
  Button button_2 (.out(button_2_out));
  // DipSwitch #(.NSwitches(1)) dipswitch_3: pin names not known; wires that end beside it: dipswitch_3_p1
  or or_1 (or_1_out, button_2_out, dipswitch_3_p1);
  buf buffer_1 (buffer_1_out, dipswitch_1_p1);
  // Switch switch_1: pin names not known; wires that end beside it: 1'b1, switch_1_p2
  buf buffer_2 (A_RST, control_logic_1_clo[26]);
  buf buffer_3 (A_IN, control_logic_1_clo[28]);
  buf buffer_4 (B_OUT, control_logic_1_clo[24]);
  buf buffer_5 (PCE, control_logic_1_clo[30]);
  buf buffer_6 (PC_OUT, control_logic_1_clo[31]);
  buf buffer_7 (B_IN, control_logic_1_clo[25]);
  buf buffer_8 (J, control_logic_1_clo[29]);
  buf buffer_9 (A_OUT, control_logic_1_clo[27]);
  // Switch switch_2: pin names not known; wires that end beside it: 1'b1, switch_2_p2
  Button button_3 (.out(ram_1_bus_2[17]));
  Pull_Resistor pull_resistor_1 (.node(MA_IN));
  Pull_Resistor pull_resistor_2 (.node(dipswitch_1_p1));
  PLEX_18 plex_18_1 (
    .B18_1(ram_1_bus_2), .B18_2({undriven, program_rom_1_data}), .B18_SEL(dipswitch_1_p1),
    .B18_3(plex_18_1_b18_3));
  buf buffer_10 (buffer_1_out, M_IN);
  Pull_Resistor pull_resistor_3 (.node(I_IN));
  buf buffer_11 (F_IN, control_logic_1_clo[20]);
  buf buffer_12 (TWOS, control_logic_1_clo[16]);
  buf buffer_13 (O_IN, control_logic_1_clo[18]);
  buf buffer_14 (SU, control_logic_1_clo[22]);
  buf buffer_15 (E_OUT, control_logic_1_clo[19]);
  buf buffer_16 (B_RST, control_logic_1_clo[23]);
  buf buffer_17 (O_RST, control_logic_1_clo[17]);
  buf buffer_18 (F_RST, control_logic_1_clo[21]);
  CLOCK clock_1 (.CLK_SWITCH(switch_2_p2), .CLK_STEP(or_1_out), .CLK(ram_1_bus_2[16]), .HALT(HALT));
  RAM_ADDR_REGISTER ram_addr_register_1 (
    .BUS(ram_1_bus_2), .MA_IN(MA_IN), .MA_RST(MA_RST), .RAM_BUS(ram_addr_register_1_ram_bus));
  PLEX_16 plex_16_1 (
    .B16_1(ram_addr_register_1_ram_bus), .B16_2(program_rom_1_addr), .B16_SEL(dipswitch_1_p1),
    .B16_3(plex_16_1_b16_3));
  DotMatrix #(.matrixcols(1), .matrixrows(16)) dotmatrix_4 (.col0(plex_16_1_b16_3));
  RAM ram_1 (
    .BUS(plex_18_1_b18_3), .RAM_BUS(plex_16_1_b16_3), .M_IN(buffer_1_out), .M_OUT(M_OUT),
    .BUS_2(ram_1_bus_2), .COPY_CLK(and_1_out));
  REGISTER register_1 (
    .BUS(ram_1_bus_2), .IN(I_IN), .OUT(I_OUT), .RST(I_RST), .A_BUS({register_1_a_bus_2, register_1_a_bus}),
    .LEDS(register_1_leds), .BUS_2(ram_1_bus_2));
  DotMatrix #(.matrixcols(1), .matrixrows(16)) dotmatrix_5 (.col0(register_1_leds));
  DotMatrix #(.inputtype("row"), .matrixcols(4), .matrixrows(1)) dotmatrix_6 (.row0(control_logic_1_step));
  CONTROL_LOGIC control_logic_1 (
    .BUS(ram_1_bus_2), .ZF(CF), .CF(ZF), .CLC_RST(CLC_RST), .I_BUS(register_1_a_bus_2),
    .CLO(control_logic_1_clo), .AUTO(switch_1_p2), .STEP(control_logic_1_step));
  buf buffer_19 (I_OUT, control_logic_1_clo[10]);
  buf buffer_20 (M_OUT, control_logic_1_clo[12]);
  buf buffer_21 (MA_RST, control_logic_1_clo[14]);
  buf buffer_22 (CLC_RST, control_logic_1_clo[8]);
  buf buffer_23 (MA_IN, control_logic_1_clo[15]);
  buf buffer_24 (I_IN, control_logic_1_clo[11]);
  buf buffer_25 (M_IN, control_logic_1_clo[13]);
  buf buffer_26 (I_RST, control_logic_1_clo[9]);
  DotMatrix #(.inputtype("row"), .matrixcols(16), .matrixrows(1)) dotmatrix_7 (.row0(ram_1_bus_2[15:0]));
  buf buffer_27 (buffer_27_out, control_logic_1_clo[6]);
  buf buffer_28 (buffer_28_out, control_logic_1_clo[0]);
  buf buffer_29 (buffer_29_out, control_logic_1_clo[2]);
  buf buffer_30 (buffer_30_out, control_logic_1_clo[4]);
  Pull_Resistor pull_resistor_4 (.node(HALT));
  buf buffer_31 (buffer_31_out, control_logic_1_clo[3]);
  buf buffer_32 (buffer_32_out, control_logic_1_clo[1]);
  buf buffer_33 (buffer_33_out, control_logic_1_clo[5]);
  buf buffer_34 (HALT, control_logic_1_clo[7]);
  Pull_Resistor pull_resistor_5 (.node(PC_OUT));
  Pull_Resistor pull_resistor_6 (.node(A_OUT));
  Pull_Resistor pull_resistor_7 (.node(E_OUT));
  ALU alu_1 (
    .BUS(ram_1_bus_2), .A_BUS(gen_register_1_a_bus), .B_BUS(gen_register_2_a_bus), .SU(SU), .F_RST(F_RST),
    .F_IIN(F_IN), .E_OUT(E_OUT), .BUS_2(ram_1_bus_2), .ZF(ZF), .CF(CF), .LEDS(alu_1_leds));
  OUTPUT_7SEGMENT output_7segment_1 (
    .BUS(ram_1_bus_2), .O_IN(O_IN), .O_RST(O_RST), .TWOS(TWOS), ._7SEGMENT(output_7segment_1__7segment),
    .NEG(output_7segment_1_neg));
  PROGRAM_COUNTER program_counter_1 (
    .BUS(ram_1_bus_2), .PC_OUT(PC_OUT), .PCE(PCE), .J(J), .BUS_2(ram_1_bus_2), .LEDS(program_counter_1_leds));
  DotMatrix #(.matrixcols(1), .matrixrows(16)) dotmatrix_8 (.col0(program_counter_1_leds));
  GEN_REGISTER gen_register_1 (
    .BUS(ram_1_bus_2), .IN(A_IN), .OUT(A_OUT), .RST(A_RST), .BUS_2(ram_1_bus_2),
    .A_BUS(gen_register_1_a_bus), .LEDS(gen_register_1_leds));
  DotMatrix #(.matrixcols(1), .matrixrows(16)) dotmatrix_9 (.col0(gen_register_1_leds));
  DotMatrix #(.matrixcols(1), .matrixrows(16)) dotmatrix_10 (.col0(gen_register_2_leds));
  DotMatrix #(.matrixcols(2), .matrixrows(1)) dotmatrix_11 (.col0(CF), .col1(ZF));
  DotMatrix #(.matrixcols(1), .matrixrows(16)) dotmatrix_12 (.col0(alu_1_leds));
  Pull_Resistor pull_resistor_8 (.node(B_RST));
  _7_Segment_Display u_7_segment_display_1 (
    .g(output_7segment_1_neg), .f(1'b0), .a(1'b0), .b(1'b0), .d(1'b0), .c(1'b0), .dp(1'b0));  // open: e
  _7_Segment_Display u_7_segment_display_2 (
    .g(output_7segment_1__7segment[3]), .f(output_7segment_1__7segment[2]),
    .a(output_7segment_1__7segment[1]), .b(output_7segment_1__7segment[0]),
    .e(output_7segment_1__7segment[7]), .d(output_7segment_1__7segment[6]),
    .c(output_7segment_1__7segment[5]), .dp(output_7segment_1__7segment[4]));
  GEN_REGISTER gen_register_2 (
    .BUS(ram_1_bus_2), .IN(B_IN), .OUT(B_OUT), .RST(B_RST), .BUS_2(ram_1_bus_2),
    .A_BUS(gen_register_2_a_bus), .LEDS(gen_register_2_leds));
  _7_Segment_Display u_7_segment_display_3 (
    .g(output_7segment_1__7segment[19]), .f(output_7segment_1__7segment[18]),
    .a(output_7segment_1__7segment[17]), .b(output_7segment_1__7segment[16]),
    .e(output_7segment_1__7segment[23]), .d(output_7segment_1__7segment[22]),
    .c(output_7segment_1__7segment[21]), .dp(output_7segment_1__7segment[20]));
  _7_Segment_Display u_7_segment_display_4 (
    .g(output_7segment_1__7segment[11]), .f(output_7segment_1__7segment[10]),
    .a(output_7segment_1__7segment[9]), .b(output_7segment_1__7segment[8]),
    .e(output_7segment_1__7segment[15]), .d(output_7segment_1__7segment[14]),
    .c(output_7segment_1__7segment[13]), .dp(output_7segment_1__7segment[12]));
  _7_Segment_Display u_7_segment_display_5 (
    .g(output_7segment_1__7segment[27]), .f(output_7segment_1__7segment[26]),
    .a(output_7segment_1__7segment[25]), .b(output_7segment_1__7segment[24]),
    .e(output_7segment_1__7segment[31]), .d(output_7segment_1__7segment[30]),
    .c(output_7segment_1__7segment[29]), .dp(output_7segment_1__7segment[28]));

  // Notes on the sheet:
  //   CLK_STEP
  //   RESET THIS TOO
  //   RST
  //   buffer_1 drives only 1 and floats otherwise
  //   RESET THIS TOO
  //   buffer_2 drives only 1 and floats otherwise
  //   buffer_3 drives only 1 and floats otherwise
  //   buffer_4 drives only 1 and floats otherwise
  //   buffer_5 drives only 1 and floats otherwise
  //   buffer_6 drives only 1 and floats otherwise
  //   buffer_7 drives only 1 and floats otherwise
  //   buffer_8 drives only 1 and floats otherwise
  //   buffer_9 drives only 1 and floats otherwise
  //   RAM
  //   buffer_10 drives only 1 and floats otherwise
  //   CONTROL LOGIC
  //   buffer_11 drives only 1 and floats otherwise
  //   buffer_12 drives only 1 and floats otherwise
  //   buffer_13 drives only 1 and floats otherwise
  //   buffer_14 drives only 1 and floats otherwise
  //   buffer_15 drives only 1 and floats otherwise
  //   buffer_16 drives only 1 and floats otherwise
  //   buffer_17 drives only 1 and floats otherwise
  //   buffer_18 drives only 1 and floats otherwise
  //   RAM_ADDR_REG
  //   INSTRUCTION REG
  //   buffer_19 drives only 1 and floats otherwise
  //   buffer_20 drives only 1 and floats otherwise
  //   buffer_21 drives only 1 and floats otherwise
  //   buffer_22 drives only 1 and floats otherwise
  //   buffer_23 drives only 1 and floats otherwise
  //   buffer_24 drives only 1 and floats otherwise
  //   buffer_25 drives only 1 and floats otherwise
  //   buffer_26 drives only 1 and floats otherwise
  //   buffer_27 drives only 1 and floats otherwise
  //   buffer_28 drives only 1 and floats otherwise
  //   buffer_29 drives only 1 and floats otherwise
  //   buffer_30 drives only 1 and floats otherwise
  //   buffer_31 drives only 1 and floats otherwise
  //   buffer_32 drives only 1 and floats otherwise
  //   buffer_33 drives only 1 and floats otherwise
  //   buffer_34 drives only 1 and floats otherwise
  //   PROGRAM_COUNTER
  //   A_REG
  //   ALU
  //   OUTPUT
  //   B_REG
endmodule

module PROGRAM_COUNTER (
  input  [17:0] BUS,
  input  PC_OUT,
  input  PCE,
  input  J,
  output [15:0] LEDS,
  output [17:0] BUS_2
);

  wire pull_resistor_6_node;

  Pull_Resistor pull_resistor_1 (.node(PCE));
  Pull_Resistor pull_resistor_2 (.node(PC_OUT));
  Pull_Resistor pull_resistor_3 (.node(BUS[16]));
  Pull_Resistor pull_resistor_4 (.node(BUS[17]));
  Pull_Resistor pull_resistor_5 (.node(J));
  Pull_Resistor pull_resistor_6 (.node(pull_resistor_6_node));
  Counter #(.width(16), .max('hffff)) counter_1 (
    .load(J), .D(BUS[15:0]), .count(PCE), .Q(LEDS), .clk(BUS[16]), .clr(BUS[17]),
    .preset(pull_resistor_6_node), .down(pull_resistor_6_node));  // open: carry
  Pull_Resistor pull_resistor_7 (.node(LEDS));
  assign BUS_2[15:0] = PC_OUT ? LEDS : 16'bz;  // Controlled_Buffer controlled_buffer_1
endmodule

module REGISTER (
  input  [17:0] BUS,
  input  IN,
  input  OUT,
  input  RST,
  output [17:0] BUS_2,
  output [15:0] LEDS,
  output [15:0] A_BUS
);

  wire and_1_out, or_1_out, pull_resistor_3_node;
  wire [15:0] controlled_buffer_1_out;

  or or_1 (or_1_out, BUS[17], and_1_out);
  and and_1 (and_1_out, BUS[16], RST);
  Pull_Resistor pull_resistor_1 (.node(OUT));
  Pull_Resistor pull_resistor_2 (.node(IN));
  Pull_Resistor pull_resistor_3 (.node(pull_resistor_3_node));
  Register #(.width(16), .Select("low")) register_1 (
    .D(BUS[15:0]), .en(IN), .Q(A_BUS), .clk(BUS[16]), .clr(or_1_out), .cs(pull_resistor_3_node),
    .preset(pull_resistor_3_node));
  Pull_Resistor pull_resistor_4 (.node(or_1_out));
  Pull_Resistor pull_resistor_5 (.node(A_BUS));
  assign controlled_buffer_1_out = OUT ? A_BUS : 16'bz;  // Controlled_Buffer controlled_buffer_1
  assign BUS_2[15:0] = OUT ? {{8{1'b0}}, controlled_buffer_1_out[7:0]} : 16'bz;  // Controlled_Buffer controlled_buffer_2

  assign LEDS = A_BUS;
endmodule

module ALU (
  input  [17:0] BUS,
  input  [15:0] A_BUS,
  input  [15:0] B_BUS,
  input  SU,
  input  F_RST,
  input  F_IIN,
  input  E_OUT,
  output ZF,
  output CF,
  output [15:0] LEDS,
  output [17:0] BUS_2
);

  wire adder_1_cout, and_1_out, nor_1_out, or_1_out, or_2_out, pull_resistor_4_node, pull_resistor_5_node,
       pull_resistor_6_node, pull_resistor_7_node, subtractor_1_bout;
  wire [15:0] adder_1_out, subtractor_1_out;

  and and_1 (and_1_out, BUS[16], F_RST);
  Pull_Resistor pull_resistor_1 (.node(F_IIN));
  Pull_Resistor pull_resistor_2 (.node(E_OUT));
  or or_1 (or_1_out, BUS[17], and_1_out);
  Pull_Resistor pull_resistor_3 (.node(SU));
  Pull_Resistor pull_resistor_4 (.node(pull_resistor_4_node));
  Adder #(.width(16)) adder_1 (
    .a(A_BUS), .b(B_BUS), .out(adder_1_out), .cin(pull_resistor_4_node), .cout(adder_1_cout));
  Pull_Resistor pull_resistor_5 (.node(pull_resistor_5_node));
  Subtractor #(.width(16)) subtractor_1 (
    .a(A_BUS), .b(B_BUS), .out(subtractor_1_out), .bin(pull_resistor_5_node), .bout(subtractor_1_bout));
  Pull_Resistor pull_resistor_6 (.node(pull_resistor_6_node));
  Register #(.width(1), .Select("low")) register_1 (
    .D(nor_1_out), .en(F_IIN), .Q(ZF), .clk(BUS[16]), .clr(or_1_out), .cs(pull_resistor_6_node),
    .preset(pull_resistor_6_node));
  or or_2 (or_2_out, adder_1_cout, subtractor_1_bout);
  Pull_Resistor pull_resistor_7 (.node(pull_resistor_7_node));
  Register #(.width(1), .Select("low")) register_2 (
    .D(or_2_out), .en(F_IIN), .Q(CF), .clk(BUS[16]), .clr(or_1_out), .cs(pull_resistor_7_node),
    .preset(pull_resistor_7_node));
  Multiplexer #(.width(16), .enable("false")) multiplexer_1 (
    .in0(adder_1_out), .in1(subtractor_1_out), .out(LEDS), .sel(SU));
  Pull_Resistor pull_resistor_8 (.node(LEDS));
  assign BUS_2[15:0] = E_OUT ? LEDS : 16'bz;  // Controlled_Buffer controlled_buffer_1
  nor nor_1 (nor_1_out, LEDS[15], LEDS[14], LEDS[13], LEDS[12], LEDS[11], LEDS[10], LEDS[9], LEDS[8], LEDS[7], LEDS[6], LEDS[5], LEDS[4], LEDS[3], LEDS[2], LEDS[1], LEDS[0]);
endmodule

module BUS_DIPSWITCH (
  input  [15:0] BUS_IN,
  input  DISCONNECT,
  output [15:0] BUS_OUT
);

  Pull_Resistor pull_resistor_1 (.node(DISCONNECT));
  Pull_Resistor pull_resistor_2 (.node(BUS_IN[2]));
  Pull_Resistor pull_resistor_3 (.node(BUS_IN[5]));
  Pull_Resistor pull_resistor_4 (.node(BUS_IN[3]));
  Pull_Resistor pull_resistor_5 (.node(BUS_IN[7]));
  Pull_Resistor pull_resistor_6 (.node(BUS_IN[1]));
  Pull_Resistor pull_resistor_7 (.node(BUS_IN[6]));
  Pull_Resistor pull_resistor_8 (.node(BUS_IN[4]));
  Pull_Resistor pull_resistor_9 (.node(BUS_IN[0]));
  // Ttl74125 ttl74125_1: pin names not known; wires that end beside it: DISCONNECT, DISCONNECT, BUS_IN[15], BUS_IN[0], BUS_OUT[15], BUS_OUT[0], DISCONNECT
  Pull_Resistor pull_resistor_10 (.node(BUS_IN[10]));
  Pull_Resistor pull_resistor_11 (.node(BUS_IN[11]));
  Pull_Resistor pull_resistor_12 (.node(BUS_IN[12]));
  Pull_Resistor pull_resistor_13 (.node(BUS_IN[15]));
  Pull_Resistor pull_resistor_14 (.node(BUS_IN[14]));
  Pull_Resistor pull_resistor_15 (.node(BUS_IN[8]));
  Pull_Resistor pull_resistor_16 (.node(BUS_IN[13]));
  Pull_Resistor pull_resistor_17 (.node(BUS_IN[9]));
  // Ttl74125 ttl74125_2: pin names not known; wires that end beside it: DISCONNECT, BUS_IN[14], BUS_IN[1], BUS_OUT[14], BUS_OUT[1], DISCONNECT, DISCONNECT, BUS_IN[13], BUS_IN[2], BUS_OUT[13], BUS_OUT[2], DISCONNECT
  // Ttl74125 ttl74125_3: pin names not known; wires that end beside it: DISCONNECT, BUS_IN[12], BUS_IN[3], BUS_OUT[12], BUS_OUT[3], DISCONNECT, DISCONNECT, BUS_IN[11], BUS_IN[4], BUS_OUT[11], BUS_OUT[4], DISCONNECT
  // Ttl74125 ttl74125_4: pin names not known; wires that end beside it: DISCONNECT, BUS_IN[10], BUS_IN[5], BUS_OUT[10], BUS_OUT[5], DISCONNECT, DISCONNECT, BUS_IN[9], BUS_IN[6], BUS_OUT[9], BUS_OUT[6], DISCONNECT, DISCONNECT, BUS_IN[8], BUS_IN[7], BUS_OUT[8], BUS_OUT[7]

  // Other names for the same wires on the sheet: M0 = BUS_IN[0]; M1 = BUS_IN[1]; M2 = BUS_IN[2]; M3 = BUS_IN[3];
  //   M4 = BUS_IN[4]; M5 = BUS_IN[5]; M6 = BUS_IN[6]; M7 = BUS_IN[7]; M8 = BUS_IN[8]; M9 = BUS_IN[9];
  //   M10 = BUS_IN[10]; M11 = BUS_IN[11]; M12 = BUS_IN[12]; M13 = BUS_IN[13]; M14 = BUS_IN[14]; M15 = BUS_IN[15]
endmodule

module OUTPUT_7SEGMENT (
  input  [17:0] BUS,
  input  O_IN,
  input  O_RST,
  input  TWOS,
  output [31:0] _7SEGMENT,
  output NEG
);

  wire and_2_out, or_1_out, pull_resistor_4_node, pull_resistor_5_node;
  wire [15:0] register_1_q;

  Pull_Resistor pull_resistor_1 (.node(O_IN));
  Pull_Resistor pull_resistor_2 (.node(O_RST));
  Pull_Resistor pull_resistor_3 (.node(TWOS));
  // AND_Gate and_1 is placed but not wired
  or or_1 (or_1_out, BUS[17], and_2_out);
  and and_2 (and_2_out, BUS[16], O_RST);
  Pull_Resistor pull_resistor_4 (.node(pull_resistor_4_node));
  Register #(.width(16), .Select("low")) register_1 (
    .D(BUS[15:0]), .en(O_IN), .Q(register_1_q), .clk(BUS[16]), .clr(or_1_out), .cs(pull_resistor_4_node),
    .preset(pull_resistor_4_node));
  Pull_Resistor pull_resistor_5 (.node(pull_resistor_5_node));
  ROM #(.addrWidth(17), .dataWidth(32), .Select("low")) rom_1 (
    .addr({TWOS, register_1_q}), .data(_7SEGMENT), .sel(pull_resistor_5_node));

  assign NEG = TWOS;

  // Notes on the sheet:
  //   NEG
  //   contents of rom_1 (hex, n*v repeats v):
  //   e7000000 21000000 cb000000 6b000000 2d000000 6e000000 ee000000 23000000 ef000000 6f000000 af000000
  //   ec000000 c6000000 e9000000 ce000000 8e000000 e7210000 21210000 cb210000 6b210000 2d210000 6e210000
  //   ee210000 23210000 ef210000 6f210000 af210000 ec210000 c6210000 e9210000 ce210000 8e210000 e7cb0000
  //   21cb0000 cbcb0000 6bcb0000 2dcb0000 6ecb0000 eecb0000 23cb0000 efcb0000 6fcb0000 afcb0000 eccb0000
  //   c6cb0000 e9cb0000 cecb0000 8ecb0000 e76b0000 216b0000 cb6b0000 6b6b0000 2d6b0000 6e6b0000 ee6b0000
  //   236b0000 ef6b0000 6f6b0000 af6b0000 ec6b0000 c66b0000 e96b0000 ce6b0000 8e6b0000 e72d0000 212d0000
  //   cb2d0000 6b2d0000 2d2d0000 6e2d0000 ee2d0000 232d0000 ef2d0000 6f2d0000 af2d0000 ec2d0000 c62d0000
  //   e92d0000 ce2d0000 8e2d0000 e76e0000 216e0000 cb6e0000 6b6e0000 2d6e0000 6e6e0000 ee6e0000 236e0000
  //   ef6e0000 6f6e0000 af6e0000 ec6e0000 c66e0000 e96e0000 ce6e0000 8e6e0000 e7ee0000 21ee0000 cbee0000
  //   6bee0000 2dee0000 6eee0000 eeee0000 23ee0000 efee0000 6fee0000 afee0000 ecee0000 c6ee0000 e9ee0000
  //   ceee0000 8eee0000 e7230000 21230000 cb230000 6b230000 2d230000 6e230000 ee230000 23230000 ef230000
  //   6f230000 af230000 ec230000 c6230000 e9230000 ce230000 8e230000 e7ef0000 21ef0000 cbef0000 6bef0000
  //   2def0000 6eef0000 eeef0000 23ef0000 efef0000 6fef0000 afef0000 ecef0000 c6ef0000 e9ef0000 ceef0000
  //   8eef0000 e76f0000 216f0000 cb6f0000 6b6f0000 2d6f0000 6e6f0000 ee6f0000 236f0000 ef6f0000 6f6f0000
  //   af6f0000 ec6f0000 c66f0000 e96f0000 ce6f0000 8e6f0000 e7af0000 21af0000 cbaf0000 6baf0000 2daf0000
  //   6eaf0000 eeaf0000 23af0000 efaf0000 6faf0000 afaf0000 ecaf0000 c6af0000 e9af0000 ceaf0000 8eaf0000
  //   e7ec0000 21ec0000 cbec0000 6bec0000 2dec0000 6eec0000 eeec0000 23ec0000 efec0000 6fec0000 afec0000
  //   ecec0000 c6ec0000 e9ec0000 ceec0000 8eec0000 e7c60000 21c60000 cbc60000 6bc60000 2dc60000 6ec60000
  //   eec60000 23c60000 efc60000 6fc60000 afc60000 ecc60000 c6c60000 e9c60000 cec60000 8ec60000 e7e90000
  //   21e90000 cbe90000 6be90000 2de90000 6ee90000 eee90000 23e90000 efe90000 6fe90000 afe90000 ece90000
  //   c6e90000 e9e90000 cee90000 8ee90000 e7ce0000 21ce0000 cbce0000 6bce0000 2dce0000 6ece0000 eece0000
  //   23ce0000 efce0000 6fce0000 afce0000 ecce0000 c6ce0000 e9ce0000 cece0000 8ece0000 e78e0000 218e0000
  //   cb8e0000 6b8e0000 2d8e0000 6e8e0000 ee8e0000 238e0000 ef8e0000 6f8e0000 af8e0000 ec8e0000 c68e0000
  //   e98e0000 ce8e0000 8e8e0000 e7e72100 21e72100 cbe72100 6be72100 2de72100 6ee72100 eee72100 23e72100
  //   efe72100 6fe72100 afe72100 ece72100 c6e72100 e9e72100 cee72100 8ee72100 e7212100 21212100 cb212100
  //   6b212100 2d212100 6e212100 ee212100 23212100 ef212100 6f212100 af212100 ec212100 c6212100 e9212100
  //   ce212100 8e212100 e7cb2100 21cb2100 cbcb2100 6bcb2100 2dcb2100 6ecb2100 eecb2100 23cb2100 efcb2100
  //   6fcb2100 afcb2100 eccb2100 c6cb2100 e9cb2100 cecb2100 8ecb2100 e76b2100 216b2100 cb6b2100 6b6b2100
  //   2d6b2100 6e6b2100 ee6b2100 236b2100 ef6b2100 6f6b2100 af6b2100 ec6b2100 c66b2100 e96b2100 ce6b2100
  //   8e6b2100 e72d2100 212d2100 cb2d2100 6b2d2100 2d2d2100 6e2d2100 ee2d2100 232d2100 ef2d2100 6f2d2100
  //   af2d2100 ec2d2100 c62d2100 e92d2100 ce2d2100 8e2d2100 e76e2100 216e2100 cb6e2100 6b6e2100 2d6e2100
  //   6e6e2100 ee6e2100 236e2100 ef6e2100 6f6e2100 af6e2100 ec6e2100 c66e2100 e96e2100 ce6e2100 8e6e2100
  //   e7ee2100 21ee2100 cbee2100 6bee2100 2dee2100 6eee2100 eeee2100 23ee2100 efee2100 6fee2100 afee2100
  //   ecee2100 c6ee2100 e9ee2100 ceee2100 8eee2100 e7232100 21232100 cb232100 6b232100 2d232100 6e232100
  //   ee232100 23232100 ef232100 6f232100 af232100 ec232100 c6232100 e9232100 ce232100 8e232100 e7ef2100
  //   21ef2100 cbef2100 6bef2100 2def2100 6eef2100 eeef2100 23ef2100 efef2100 6fef2100 afef2100 ecef2100
  //   c6ef2100 e9ef2100 ceef2100 8eef2100 e76f2100 216f2100 cb6f2100 6b6f2100 2d6f2100 6e6f2100 ee6f2100
  //   236f2100 ef6f2100 6f6f2100 af6f2100 ec6f2100 c66f2100 e96f2100 ce6f2100 8e6f2100 e7af2100 21af2100
  //   cbaf2100 6baf2100 2daf2100 6eaf2100 eeaf2100 23af2100 efaf2100 6faf2100 afaf2100 ecaf2100 c6af2100
  //   e9af2100 ceaf2100 8eaf2100 e7ec2100 21ec2100 cbec2100 6bec2100 2dec2100 6eec2100 eeec2100 23ec2100
  //   efec2100 6fec2100 afec2100 ecec2100 c6ec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
endmodule

module RAM_ADDR_REGISTER (
  input  [17:0] BUS,
  input  MA_IN,
  input  MA_RST,
  output [15:0] RAM_BUS
);

  wire and_1_out, or_1_out, pull_resistor_1_node;

  or or_1 (or_1_out, BUS[17], and_1_out);
  and and_1 (and_1_out, BUS[16], MA_RST);
  Pull_Resistor pull_resistor_1 (.node(pull_resistor_1_node));
  Register #(.width(16), .Select("low")) register_1 (
    .D(BUS[15:0]), .en(MA_IN), .Q(RAM_BUS), .clk(BUS[16]), .clr(or_1_out), .cs(pull_resistor_1_node),
    .preset(pull_resistor_1_node));
endmodule

module RAM (
  input  [17:0] BUS,
  input  [15:0] RAM_BUS,
  input  M_IN,
  input  M_OUT,
  input  COPY_CLK,
  output [17:0] BUS_2
);

  wire and_1_out, not_1_out, pull_resistor_1_node, pull_resistor_3_node;
  wire [15:0] controlled_buffer_1_out;

  Pull_Resistor pull_resistor_1 (.node(pull_resistor_1_node));
  buf buffer_1 (pull_resistor_1_node, BUS[16]);
  Pull_Resistor pull_resistor_2 (.node(M_IN));
  buf buffer_2 (pull_resistor_1_node, COPY_CLK);
  and and_1 (and_1_out, pull_resistor_1_node, M_IN);
  Pull_Resistor pull_resistor_3 (.node(pull_resistor_3_node));
  Pull_Resistor pull_resistor_4 (.node(M_OUT));
  not not_1 (not_1_out, M_OUT);
  assign controlled_buffer_1_out = not_1_out ? BUS[15:0] : 16'bz;  // Controlled_Buffer controlled_buffer_1
  RAM_part #(.addrWidth(16), .dataWidth(16), .Select("low")) ram_1 (
    .addr(RAM_BUS), .data(controlled_buffer_1_out), .sel(pull_resistor_3_node), .clk(and_1_out), .ld(M_OUT));  // open: clr
  assign BUS_2[15:0] = M_OUT ? controlled_buffer_1_out : 16'bz;  // Controlled_Buffer controlled_buffer_2

  // Notes on the sheet:
  //   buffer_1 drives only 1 and floats otherwise
  //   buffer_2 drives only 1 and floats otherwise
endmodule

module CONTROL_LOGIC (
  input  [17:0] BUS,
  input  ZF,
  input  CF,
  input  CLC_RST,
  input  [7:0] I_BUS,
  input  AUTO,
  output [3:0] STEP,
  output [31:0] CLO
);

  wire not_1_out, or_1_out, pull_resistor_3_node;
  wire [31:0] rom_1_data;

  Pull_Resistor pull_resistor_1 (.node(CLC_RST));
  // AND_Gate and_1 has open pins: in0=BUS[16], out=open
  Pull_Resistor pull_resistor_2 (.node(AUTO));
  not not_1 (not_1_out, BUS[16]);
  or or_1 (or_1_out, BUS[17], CLC_RST);
  Pull_Resistor pull_resistor_3 (.node(pull_resistor_3_node));
  Counter #(.width(4), .max('hf)) counter_1 (
    .load(1'b0), .count(1'b1), .Q(STEP), .clk(not_1_out), .clr(or_1_out), .preset(1'b0), .down(1'b0));  // open: D, carry
  ROM #(.addrWidth(14), .dataWidth(32), .Select("low")) rom_1 (
    .addr({I_BUS, STEP, CF, ZF}), .data(rom_1_data), .sel(pull_resistor_3_node));
  assign CLO = AUTO ? rom_1_data : 32'bz;  // Controlled_Buffer controlled_buffer_1

  // Notes on the sheet:
  //   contents of rom_1 (hex, n*v repeats v):
  //   4*80008000 4*40001800 4*100 52*0 4*80008000 4*40001800 4*11000000 4*100 48*0 4*80008000 4*40001800
  //   4*10000400 4*100 48*0 4*80008000 4*40001800 4*4000 4*8400 4*10001000 4*100 40*0 4*80008000
  //   4*40001800 4*8008000 4*1002000 4*100 44*0 4*80008000 4*40001800 4*8008000 4*8400 4*100 44*0
  //   4*80008000 4*40001800 4*100 52*0 4*80008000 4*40001800 4*a000000 4*100 48*0 4*80008000 4*40001800
  //   4*2000400 4*100 48*0 4*80008000 4*40001800 4*4000 4*8400 4*2001000 4*100 40*0 4*80008000 4*40001800
  //   4*1008000 4*8002000 4*100 44*0 4*80008000 4*40001800 4*1008000 4*8400 4*100 44*0 4*80008000
  //   4*40001800 4*100 52*0 4*80008000 4*40001800 4*4000 4*8400 4*8002000 4*100 40*0 4*80008000 4*40001800
  //   4*4000 4*8400 4*1002000 4*100 40*0 4*80008000 4*40001800 4*100 52*0 4*80008000 4*40001800 4*100 52*0
  //   4*80008000 4*40001800 4*200000 4*10180000 4*100 44*0 4*80008000 4*40001800 4*2200400 4*10180000
  //   4*100 44*0 4*80008000 4*40001800 4*204000 4*8400 4*2001000 4*10180000 4*100 36*0 4*80008000
  //   4*40001800 4*200000 4*10580000 4*100 44*0 4*80008000 4*40001800 4*2200400 4*10580000 4*100 44*0
  //   4*80008000 4*40001800 4*204000 4*8400 4*2001000 4*10580000 4*100 36*0 4*80008000 4*40001800
  //   4*60200400 4*100 48*0 4*80008000 4*40001800 40200000 60200400 40200000 60200400 4*100 48*0
  //   4*80008000 4*40001800 40200000 40200000 60200400 60200400 4*100 48*0 4*80008000 4*40001800 4*200000
  //   4*100000 4*100 44*0 4*80008000 4*40001800 4*200000 4*2000400 4*100000 4*100 40*0 4*80008000
  //   4*40001800 4*100 52*0 4*80008000 4*40001800 4*100 52*0 4*80008000 4*40001800 200000 200000 20200400
  //   20200400 4*100 48*0 4*80008000 4*40001800 100 20200400 20200400 20200400 0 100 100 100 48*0
  //   4*80008000 4*40001800 100 20200400 100 20200400 0 100 0 100 48*0 4*80008000 4*40001800 20200400
  //   20200400 100 20200400 100 100 0 100 48*0 4*80008000 4*40001800 20200400 4*100 51*0 4*80008000
  //   4*40001800 4*100 52*0 4*80008000 4*40001800 4*8040000 4*100 48*0 4*80008000 4*40001800 4*1040000
  //   4*100 48*0 4*80008000 4*40001800 4*40400 4*100 48*0 4*80008000 4*40001800 4*4000 4*8400 4*41000
  //   4*100 40*0 4*80008000 4*40001800 4*100 52*0 4*80008000 4*40001800 4*100 52*0 4*80008000 4*40001800
  //   4*100 52*0 4*80008000 4*40001800 4*100 52*0 4*80008000 4*40001800 4*100 52*0 4*80008000 4*40001800
  //   4*100 52*0 4*80008000 4*40001800 4*100 52*0 4*80008000 4*40001800 4*100 52*0 4*80008000 4*40001800
  //   4*100 52*0 4*80008000 4*40001800 4*100 52*0 4*80008000 4*40001800 4*100 52*0 4*80008000 4*40001800
  //   4*100 52*0 4*80008000 4*40001800 4*100 52*0 4*80008000 4*40001800 4*100 52*0 4*80008000 4*40001800
  //   4*100 52*0 4*80008000 4*40001800 4*100 52*0 4*80008000 4*40001800 4*100 52*0 4*80008000 4*40001800
  //   4*100 52*0 4*80008000 4*40001800 4*100 52*0 4*80008000 4*40001800 4*100 52*0 4*80008000 4*40001800
  //   4*100 52*0 4*80008000 4*40001800 4*100 52*0 4*80008000 4*40001800 4*100 52*0 4*80008000 4*40001800
  //   4*100 52*0 4*80008000 4*40001800 4*100 52*0 4*80008000 4*40001800 4*100 52*0 4*80008000 4*40001800
  //   4*100 52*0 4*80008000 4*40001800 4*100 52*0 4*80008000 4*40001800 4*100 52*0 4*80008000 4*40001800
  //   4*100 52*0 4*80008000 4*40001800 4*100 52*0 4*80008000 4*40001800 4*100 52*0 4*80008000 4*40001800
  //   4*100 52*0 4*80008000 4*40001800 4*100 52*0 4*80008000 4*40001800 4*100 52*0 4*80008000 4*40001800
  //   4*100 52*0 4*80008000 4*40001800 4*100 52*0 4*80008000 4*40001800 4*100 52*0 4*80008000 4*40001800
  //   4*100 52*0 4*80008000 4*40001800 4*100 52*0 4*80008000 4*40001800 4*100 52*0 4*80008000 4*40001800
  //   4*100 52*0 4*80008000 4*40001800 4*100 52*0 4*80008000 4*40001800 4*100 52*0 4*80008000 4*40001800
  //   4*100 52*0 4*80008000 4*40001800 4*100 52*0 4*80008000 4*40001800 4*100 52*0 4*80008000 4*40001800
  //   4*100 52*0 4*80008000 4*40001800 4*100 52*0 4*80008000 4*40001800 4*100 52*0 4*80008000 4*40001800
  //   4*100 52*0 4*80008000 4*40001800 4*100 52*0 4*80008000 4*40001800 4*100 52*0 4*80008000 4*40001800
  //   4*100 52*0 4*80008000 4*40001800 4*100 52*0 4*80008000 4*40001800 4*100 52*0 4*80008000 4*40001800
  //   4*100 52*0 4*80008000 4*40001800 4*100 52*0 4*80008000 4*40001800 4*100 52*0 4*80008000 4*40001800
  //   4*100 52*0 4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
endmodule

module PROGRAM_ROM (
  input  ENB,
  input  R_CLK,
  input  R_RST,
  output DONE,
  output [15:0] ADDR,
  output [15:0] DATA
);

  wire and_1_out, and_2_out, buffer_1_out, counter_1_carry, not_1_out, pull_resistor_1_node;

  not not_1 (not_1_out, DONE);
  and and_1 (and_1_out, not_1_out, R_CLK);
  Pull_Resistor pull_resistor_1 (.node(pull_resistor_1_node));
  Counter #(.width(16), .max('hffff)) counter_1 (
    .load(1'b0), .count(ENB), .Q(ADDR), .carry(counter_1_carry), .clk(and_1_out), .clr(R_RST), .preset(1'b0),
    .down(1'b0));  // open: D
  ROM #(.addrWidth(16), .dataWidth(16), .Select("low")) rom_1 (.addr(ADDR), .data(DATA), .sel(pull_resistor_1_node));
  buf buffer_1 (buffer_1_out, counter_1_carry);
  and and_2 (and_2_out, R_CLK, buffer_1_out);
  D_Flip_Flop d_ff_1 (.clk(and_2_out), .D(buffer_1_out), .Q(DONE), .preset(1'b0), .reset(R_RST));  // open: Qn
  and and_3 (buffer_1_out, DATA[0], DATA[1], DATA[2], DATA[3], DATA[4], DATA[5], DATA[6], DATA[7], DATA[8], DATA[9], DATA[10], DATA[11], DATA[12], DATA[13], DATA[14], DATA[15]);

  // Notes on the sheet:
  //   contents of rom_1 (hex, n*v repeats v):
  //   200 801 2400 1100 2400 1703 ff00 ffff
  //   buffer_1 drives only 1 and floats otherwise
endmodule

module PLEX_16 (
  input  [15:0] B16_1,
  input  [15:0] B16_2,
  input  B16_SEL,
  output [15:0] B16_3
);

  Multiplexer #(.width(16), .enable("false")) multiplexer_1 (.in0(B16_1), .in1(B16_2), .out(B16_3), .sel(B16_SEL));
endmodule

module PLEX_18 (
  input  [17:0] B18_1,
  input  [17:0] B18_2,
  input  B18_SEL,
  output [17:0] B18_3
);

  Multiplexer #(.width(18), .enable("false")) multiplexer_1 (.in0(B18_1), .in1(B18_2), .out(B18_3), .sel(B18_SEL));
endmodule

module GEN_REGISTER (
  input  [17:0] BUS,
  input  IN,
  input  OUT,
  input  RST,
  output [17:0] BUS_2,
  output [15:0] LEDS,
  output [15:0] A_BUS
);

  wire and_1_out, or_1_out, pull_resistor_2_node;

  or or_1 (or_1_out, BUS[17], and_1_out);
  and and_1 (and_1_out, BUS[16], RST);
  Pull_Resistor pull_resistor_1 (.node(OUT));
  Pull_Resistor pull_resistor_2 (.node(pull_resistor_2_node));
  Register #(.width(16), .Select("low")) register_1 (
    .D(BUS[15:0]), .en(IN), .Q(A_BUS), .clk(BUS[16]), .clr(or_1_out), .cs(pull_resistor_2_node),
    .preset(pull_resistor_2_node));
  Pull_Resistor pull_resistor_3 (.node(IN));
  Pull_Resistor pull_resistor_4 (.node(or_1_out));
  Pull_Resistor pull_resistor_5 (.node(A_BUS));
  assign BUS_2[15:0] = OUT ? A_BUS : 16'bz;  // Controlled_Buffer controlled_buffer_1

  assign LEDS = A_BUS;
endmodule
