// Logisim project 16BitCPU.circ as structural Verilog: 14 circuits, main circuit main
module CLOCK (
  input  HALT,
  input  CLK_SWITCH,
  input  CLK_STEP,
  output CLK
);

  wire and_1_out, and_2_out, clock_1_out, not_1_out, not_2_out, or_1_out;

  Clock clock_1 (.out(clock_1_out));
  Pull_Resistor pull_resistor_1 (.node(CLK_SWITCH));
  Pull_Resistor pull_resistor_2 (.node(CLK_STEP));
  and and_1 (and_1_out, clock_1_out, not_1_out);
  not not_1 (not_1_out, CLK_SWITCH);
  and and_2 (and_2_out, CLK_SWITCH, CLK_STEP);
  not not_2 (not_2_out, HALT);
  or or_1 (or_1_out, and_1_out, and_2_out);
  and and_3 (CLK, not_2_out, or_1_out);
endmodule

module main (
);

  wire A_IN, A_OUT, A_RST, and_1_out, B_IN, B_OUT, B_RST, buffer_1_out, buffer_27_out, buffer_28_out,
       buffer_29_out, buffer_30_out, buffer_31_out, buffer_32_out, buffer_34_out, button_1_out, button_2_out,
       CF, CLC_RST, clock_2_out, dipswitch_1_p1, dipswitch_2_p1, dipswitch_3_p1, E_OUT, F_IN, F_RST, HALT,
       I_IN, I_OUT, I_RST, J, M_IN, M_OUT, MA_IN, MA_RST, O_IN, O_RST, or_1_out, output_7segment_1_le_0,
       output_7segment_1_neg, PC_OUT, PCE, program_rom_1_done, SU, switch_1_p2, switch_2_p2, TWOS, ZF;
  wire [3:0] control_logic_1_step;
  wire [7:0] n7seg_dmx_1__7seg_0_7_0, n7seg_dmx_1__7seg_0_7_1, n7seg_dmx_1__7seg_8_15_0,
       n7seg_dmx_1__7seg_8_15_1, output_7segment_1__7seg_0_7, output_7segment_1__7seg_8_15, register_1_a_bus,
       register_1_a_bus_2;
  wire [15:0] alu_1_leds, gen_register_1_a_bus, gen_register_1_leds, gen_register_2_a_bus,
       gen_register_2_leds, plex_16_1_b16_3, program_counter_1_leds, program_rom_1_addr, program_rom_1_data,
       ram_addr_register_1_ram_bus, register_1_leds;
  wire [17:0] plex_18_1_b18_3, ram_1_bus_2;
  wire [17:16] undriven;
  wire [31:0] control_logic_1_clo;

  Button button_1 (.out(button_1_out));
  DotMatrix #(.inputtype("row"), .matrixcols(16), .matrixrows(1)) dotmatrix_1 (.row0(program_rom_1_addr));
  DotMatrix #(.inputtype("row"), .matrixcols(16), .matrixrows(1)) dotmatrix_2 (.row0(program_rom_1_data));
  // DipSwitch #(.NSwitches(1)) dipswitch_1: pin names not known; wires that end beside it: dipswitch_1_p1
  and and_1 (and_1_out, dipswitch_1_p1, button_1_out);
  // DipSwitch #(.NSwitches(1)) dipswitch_2: pin names not known; wires that end beside it: dipswitch_2_p1
  LED led_1 (.in(program_rom_1_done));
  PROGRAM_ROM program_rom_1 (
    .ENB(dipswitch_1_p1), .R_CLK(and_1_out), .R_RST(dipswitch_2_p1), .DONE(program_rom_1_done),
    .ADDR(program_rom_1_addr), .DATA(program_rom_1_data));
  DotMatrix #(.inputtype("row"), .matrixcols(32), .matrixrows(1)) dotmatrix_3 (.row0(control_logic_1_clo));
  Button button_2 (.out(button_2_out));
  // DipSwitch #(.NSwitches(1)) dipswitch_3: pin names not known; wires that end beside it: dipswitch_3_p1
  or or_1 (or_1_out, button_2_out, dipswitch_3_p1);
  buf buffer_1 (buffer_1_out, dipswitch_1_p1);
  // Switch switch_1: pin names not known; wires that end beside it: 1'b1, switch_1_p2
  buf buffer_2 (PCE, control_logic_1_clo[30]);
  buf buffer_3 (A_RST, control_logic_1_clo[26]);
  buf buffer_4 (A_IN, control_logic_1_clo[28]);
  buf buffer_5 (B_OUT, control_logic_1_clo[24]);
  buf buffer_6 (A_OUT, control_logic_1_clo[27]);
  buf buffer_7 (B_IN, control_logic_1_clo[25]);
  buf buffer_8 (PC_OUT, control_logic_1_clo[31]);
  buf buffer_9 (J, control_logic_1_clo[29]);
  // Switch switch_2: pin names not known; wires that end beside it: 1'b1, switch_2_p2
  Button button_3 (.out(ram_1_bus_2[17]));
  Pull_Resistor pull_resistor_1 (.node(MA_IN));
  Pull_Resistor pull_resistor_2 (.node(dipswitch_1_p1));
  PLEX_18 plex_18_1 (
    .B18_1(ram_1_bus_2), .B18_2({undriven, program_rom_1_data}), .B18_SEL(dipswitch_1_p1),
    .B18_3(plex_18_1_b18_3));
  buf buffer_10 (buffer_1_out, M_IN);
  Pull_Resistor pull_resistor_3 (.node(I_IN));
  buf buffer_11 (SU, control_logic_1_clo[22]);
  buf buffer_12 (O_IN, control_logic_1_clo[18]);
  buf buffer_13 (TWOS, control_logic_1_clo[16]);
  buf buffer_14 (F_IN, control_logic_1_clo[20]);
  buf buffer_15 (F_RST, control_logic_1_clo[21]);
  buf buffer_16 (O_RST, control_logic_1_clo[17]);
  buf buffer_17 (B_RST, control_logic_1_clo[23]);
  buf buffer_18 (E_OUT, control_logic_1_clo[19]);
  CLOCK clock_1 (.CLK_SWITCH(switch_2_p2), .CLK_STEP(or_1_out), .CLK(ram_1_bus_2[16]), .HALT(HALT));
  RAM_ADDR_REGISTER ram_addr_register_1 (
    .BUS(ram_1_bus_2), .MA_IN(MA_IN), .MA_RST(MA_RST), .RAM_BUS(ram_addr_register_1_ram_bus));
  PLEX_16 plex_16_1 (
    .B16_1(ram_addr_register_1_ram_bus), .B16_2(program_rom_1_addr), .B16_SEL(dipswitch_1_p1),
    .B16_3(plex_16_1_b16_3));
  DotMatrix #(.matrixcols(1), .matrixrows(16)) dotmatrix_4 (.col0(plex_16_1_b16_3));
  RAM ram_1 (
    .BUS(plex_18_1_b18_3), .RAM_BUS(plex_16_1_b16_3), .M_IN(buffer_1_out), .M_OUT(M_OUT),
    .BUS_2(ram_1_bus_2), .COPY_CLK(and_1_out));
  REGISTER register_1 (
    .BUS(ram_1_bus_2), .IN(I_IN), .OUT(I_OUT), .RST(I_RST), .A_BUS({register_1_a_bus_2, register_1_a_bus}),
    .LEDS(register_1_leds), .BUS_2(ram_1_bus_2));
  DotMatrix #(.matrixcols(1), .matrixrows(16)) dotmatrix_5 (.col0(register_1_leds));
  DotMatrix #(.inputtype("row"), .matrixcols(4), .matrixrows(1)) dotmatrix_6 (.row0(control_logic_1_step));
  CONTROL_LOGIC control_logic_1 (
    .BUS(ram_1_bus_2), .ZF(CF), .CF(ZF), .CLC_RST(CLC_RST), .I_BUS(register_1_a_bus_2),
    .CLO(control_logic_1_clo), .AUTO(switch_1_p2), .STEP(control_logic_1_step));
  buf buffer_19 (M_OUT, control_logic_1_clo[12]);
  buf buffer_20 (MA_RST, control_logic_1_clo[14]);
  buf buffer_21 (CLC_RST, control_logic_1_clo[8]);
  buf buffer_22 (I_OUT, control_logic_1_clo[10]);
  buf buffer_23 (M_IN, control_logic_1_clo[13]);
  buf buffer_24 (I_RST, control_logic_1_clo[9]);
  buf buffer_25 (I_IN, control_logic_1_clo[11]);
  buf buffer_26 (MA_IN, control_logic_1_clo[15]);
  DotMatrix #(.inputtype("row"), .matrixcols(16), .matrixrows(1)) dotmatrix_7 (.row0(ram_1_bus_2[15:0]));
  buf buffer_27 (buffer_27_out, control_logic_1_clo[6]);
  buf buffer_28 (buffer_28_out, control_logic_1_clo[0]);
  buf buffer_29 (buffer_29_out, control_logic_1_clo[2]);
  buf buffer_30 (buffer_30_out, control_logic_1_clo[4]);
  Pull_Resistor pull_resistor_4 (.node(HALT));
  buf buffer_31 (buffer_31_out, control_logic_1_clo[1]);
  buf buffer_32 (buffer_32_out, control_logic_1_clo[3]);
  buf buffer_33 (HALT, control_logic_1_clo[7]);
  buf buffer_34 (buffer_34_out, control_logic_1_clo[5]);
  Pull_Resistor pull_resistor_5 (.node(PC_OUT));
  Pull_Resistor pull_resistor_6 (.node(A_OUT));
  Pull_Resistor pull_resistor_7 (.node(E_OUT));
  Clock clock_2 (.out(clock_2_out));
  ALU alu_1 (
    .BUS(ram_1_bus_2), .A_BUS(gen_register_1_a_bus), .B_BUS(gen_register_2_a_bus), .SU(SU), .F_RST(F_RST),
    .F_IIN(F_IN), .E_OUT(E_OUT), .BUS_2(ram_1_bus_2), .ZF(ZF), .CF(CF), .LEDS(alu_1_leds));
  OUTPUT_7SEGMENT output_7segment_1 (
    .BUS(ram_1_bus_2), .O_IN(O_IN), .O_RST(O_RST), .TWOS(TWOS), ._7SEG_8_15(output_7segment_1__7seg_8_15),
    .NEG(output_7segment_1_neg), .LE_0(output_7segment_1_le_0), ._7SEG_0_7(output_7segment_1__7seg_0_7),
    ._7S_CLK(clock_2_out));  // open: LE_1
  _7SEG_DMX u_7seg_dmx_1 (
    ._7SEG_0_7(output_7segment_1__7seg_0_7), ._7SEG_8_15(output_7segment_1__7seg_8_15),
    .LE(output_7segment_1_le_0), ._7SEG_0_7_0(n7seg_dmx_1__7seg_0_7_0),
    ._7SEG_0_7_1(n7seg_dmx_1__7seg_0_7_1), ._7SEG_8_15_0(n7seg_dmx_1__7seg_8_15_0),
    ._7SEG_8_15_1(n7seg_dmx_1__7seg_8_15_1));
  PROGRAM_COUNTER program_counter_1 (
    .BUS(ram_1_bus_2), .PC_OUT(PC_OUT), .PCE(PCE), .J(J), .BUS_2(ram_1_bus_2), .LEDS(program_counter_1_leds));
  DotMatrix #(.matrixcols(1), .matrixrows(16)) dotmatrix_8 (.col0(program_counter_1_leds));
  GEN_REGISTER gen_register_1 (
    .BUS(ram_1_bus_2), .IN(A_IN), .OUT(A_OUT), .RST(A_RST), .BUS_2(ram_1_bus_2),
    .A_BUS(gen_register_1_a_bus), .LEDS(gen_register_1_leds));
  DotMatrix #(.matrixcols(1), .matrixrows(16)) dotmatrix_9 (.col0(gen_register_1_leds));
  DotMatrix #(.matrixcols(1), .matrixrows(16)) dotmatrix_10 (.col0(gen_register_2_leds));
  DotMatrix #(.matrixcols(2), .matrixrows(1)) dotmatrix_11 (.col0(CF), .col1(ZF));
  DotMatrix #(.matrixcols(1), .matrixrows(16)) dotmatrix_12 (.col0(alu_1_leds));
  Pull_Resistor pull_resistor_8 (.node(B_RST));
  _7_Segment_Display u_7_segment_display_1 (
    .g(n7seg_dmx_1__7seg_0_7_0[6]), .f(n7seg_dmx_1__7seg_0_7_0[5]), .a(n7seg_dmx_1__7seg_0_7_0[0]),
    .b(n7seg_dmx_1__7seg_0_7_0[1]), .e(n7seg_dmx_1__7seg_0_7_0[4]), .d(n7seg_dmx_1__7seg_0_7_0[3]),
    .c(n7seg_dmx_1__7seg_0_7_0[2]), .dp(n7seg_dmx_1__7seg_0_7_0[7]));
  _7_Segment_Display u_7_segment_display_2 (
    .g(output_7segment_1_neg), .f(1'b0), .a(1'b0), .b(1'b0), .e(1'b0), .d(1'b0), .c(1'b0), .dp(1'b0));
  GEN_REGISTER gen_register_2 (
    .BUS(ram_1_bus_2), .IN(B_IN), .OUT(B_OUT), .RST(B_RST), .BUS_2(ram_1_bus_2),
    .A_BUS(gen_register_2_a_bus), .LEDS(gen_register_2_leds));
  _7_Segment_Display u_7_segment_display_3 (
    .g(n7seg_dmx_1__7seg_0_7_1[6]), .f(n7seg_dmx_1__7seg_0_7_1[5]), .a(n7seg_dmx_1__7seg_0_7_1[0]),
    .b(n7seg_dmx_1__7seg_0_7_1[1]), .e(n7seg_dmx_1__7seg_0_7_1[4]), .d(n7seg_dmx_1__7seg_0_7_1[3]),
    .c(n7seg_dmx_1__7seg_0_7_1[2]), .dp(n7seg_dmx_1__7seg_0_7_1[7]));
  _7_Segment_Display u_7_segment_display_4 (
    .g(n7seg_dmx_1__7seg_8_15_0[6]), .f(n7seg_dmx_1__7seg_8_15_0[5]), .a(n7seg_dmx_1__7seg_8_15_0[0]),
    .b(n7seg_dmx_1__7seg_8_15_0[1]), .e(n7seg_dmx_1__7seg_8_15_0[4]), .d(n7seg_dmx_1__7seg_8_15_0[3]),
    .c(n7seg_dmx_1__7seg_8_15_0[2]), .dp(n7seg_dmx_1__7seg_8_15_0[7]));
  _7_Segment_Display u_7_segment_display_5 (
    .g(n7seg_dmx_1__7seg_8_15_1[6]), .f(n7seg_dmx_1__7seg_8_15_1[5]), .a(n7seg_dmx_1__7seg_8_15_1[0]),
    .b(n7seg_dmx_1__7seg_8_15_1[1]), .e(n7seg_dmx_1__7seg_8_15_1[4]), .d(n7seg_dmx_1__7seg_8_15_1[3]),
    .c(n7seg_dmx_1__7seg_8_15_1[2]), .dp(n7seg_dmx_1__7seg_8_15_1[7]));

  // Notes on the sheet:
  //   CLK_STEP
  //   RESET THIS TOO
  //   RST
  //   buffer_1 drives only 1 and floats otherwise
  //   RESET THIS TOO
  //   buffer_2 drives only 1 and floats otherwise
  //   buffer_3 drives only 1 and floats otherwise
  //   buffer_4 drives only 1 and floats otherwise
  //   buffer_5 drives only 1 and floats otherwise
  //   buffer_6 drives only 1 and floats otherwise
  //   buffer_7 drives only 1 and floats otherwise
  //   buffer_8 drives only 1 and floats otherwise
  //   buffer_9 drives only 1 and floats otherwise
  //   RAM
  //   buffer_10 drives only 1 and floats otherwise
  //   CONTROL LOGIC
  //   buffer_11 drives only 1 and floats otherwise
  //   buffer_12 drives only 1 and floats otherwise
  //   buffer_13 drives only 1 and floats otherwise
  //   buffer_14 drives only 1 and floats otherwise
  //   buffer_15 drives only 1 and floats otherwise
  //   buffer_16 drives only 1 and floats otherwise
  //   buffer_17 drives only 1 and floats otherwise
  //   buffer_18 drives only 1 and floats otherwise
  //   RAM_ADDR_REG
  //   INSTRUCTION REG
  //   buffer_19 drives only 1 and floats otherwise
  //   buffer_20 drives only 1 and floats otherwise
  //   buffer_21 drives only 1 and floats otherwise
  //   buffer_22 drives only 1 and floats otherwise
  //   buffer_23 drives only 1 and floats otherwise
  //   buffer_24 drives only 1 and floats otherwise
  //   buffer_25 drives only 1 and floats otherwise
  //   buffer_26 drives only 1 and floats otherwise
  //   buffer_27 drives only 1 and floats otherwise
  //   buffer_28 drives only 1 and floats otherwise
  //   buffer_29 drives only 1 and floats otherwise
  //   buffer_30 drives only 1 and floats otherwise
  //   buffer_31 drives only 1 and floats otherwise
  //   buffer_32 drives only 1 and floats otherwise
  //   buffer_33 drives only 1 and floats otherwise
  //   buffer_34 drives only 1 and floats otherwise
  //   PROGRAM_COUNTER
  //   A_REG
  //   ALU
  //   OUTPUT
  //   B_REG
endmodule

module PROGRAM_COUNTER (
  input  [17:0] BUS,
  input  PC_OUT,
  input  PCE,
  input  J,
  output [15:0] LEDS,
  output [17:0] BUS_2
);

  wire pull_resistor_6_node;

  Pull_Resistor pull_resistor_1 (.node(PC_OUT));
  Pull_Resistor pull_resistor_2 (.node(BUS[17]));
  Pull_Resistor pull_resistor_3 (.node(BUS[16]));
  Pull_Resistor pull_resistor_4 (.node(PCE));
  Pull_Resistor pull_resistor_5 (.node(J));
  Pull_Resistor pull_resistor_6 (.node(pull_resistor_6_node));
  Counter #(.width(16), .max('hffff)) counter_1 (
    .load(J), .D(BUS[15:0]), .count(PCE), .Q(LEDS), .clk(BUS[16]), .clr(BUS[17]),
    .preset(pull_resistor_6_node), .down(pull_resistor_6_node));  // open: carry
  Pull_Resistor pull_resistor_7 (.node(LEDS));
  assign BUS_2[15:0] = PC_OUT ? LEDS : 16'bz;  // Controlled_Buffer controlled_buffer_1
endmodule

module REGISTER (
  input  [17:0] BUS,
  input  IN,
  input  OUT,
  input  RST,
  output [17:0] BUS_2,
  output [15:0] LEDS,
  output [15:0] A_BUS
);

  wire and_1_out, or_1_out, pull_resistor_3_node;
  wire [15:0] controlled_buffer_1_out;

  or or_1 (or_1_out, BUS[17], and_1_out);
  and and_1 (and_1_out, BUS[16], RST);
  Pull_Resistor pull_resistor_1 (.node(OUT));
  Pull_Resistor pull_resistor_2 (.node(IN));
  Pull_Resistor pull_resistor_3 (.node(pull_resistor_3_node));
  Register #(.width(16), .Select("low")) register_1 (
    .D(BUS[15:0]), .en(IN), .Q(A_BUS), .clk(BUS[16]), .clr(or_1_out), .cs(pull_resistor_3_node),
    .preset(pull_resistor_3_node));
  Pull_Resistor pull_resistor_4 (.node(or_1_out));
  Pull_Resistor pull_resistor_5 (.node(A_BUS));
  assign controlled_buffer_1_out = OUT ? A_BUS : 16'bz;  // Controlled_Buffer controlled_buffer_1
  assign BUS_2[15:0] = OUT ? {{8{1'b0}}, controlled_buffer_1_out[7:0]} : 16'bz;  // Controlled_Buffer controlled_buffer_2

  assign LEDS = A_BUS;
endmodule

module ALU (
  input  [17:0] BUS,
  input  [15:0] A_BUS,
  input  [15:0] B_BUS,
  input  SU,
  input  F_RST,
  input  F_IIN,
  input  E_OUT,
  output ZF,
  output CF,
  output [15:0] LEDS,
  output [17:0] BUS_2
);

  wire adder_1_cout, and_1_out, nor_1_out, or_1_out, or_2_out, pull_resistor_4_node, pull_resistor_5_node,
       pull_resistor_6_node, pull_resistor_7_node, subtractor_1_bout;
  wire [15:0] adder_1_out, subtractor_1_out;

  and and_1 (and_1_out, BUS[16], F_RST);
  Pull_Resistor pull_resistor_1 (.node(F_IIN));
  Pull_Resistor pull_resistor_2 (.node(E_OUT));
  or or_1 (or_1_out, BUS[17], and_1_out);
  Pull_Resistor pull_resistor_3 (.node(SU));
  Pull_Resistor pull_resistor_4 (.node(pull_resistor_4_node));
  Adder #(.width(16)) adder_1 (
    .a(A_BUS), .b(B_BUS), .out(adder_1_out), .cin(pull_resistor_4_node), .cout(adder_1_cout));
  Pull_Resistor pull_resistor_5 (.node(pull_resistor_5_node));
  Subtractor #(.width(16)) subtractor_1 (
    .a(A_BUS), .b(B_BUS), .out(subtractor_1_out), .bin(pull_resistor_5_node), .bout(subtractor_1_bout));
  Pull_Resistor pull_resistor_6 (.node(pull_resistor_6_node));
  Register #(.width(1), .Select("low")) register_1 (
    .D(nor_1_out), .en(F_IIN), .Q(ZF), .clk(BUS[16]), .clr(or_1_out), .cs(pull_resistor_6_node),
    .preset(pull_resistor_6_node));
  or or_2 (or_2_out, adder_1_cout, subtractor_1_bout);
  Pull_Resistor pull_resistor_7 (.node(pull_resistor_7_node));
  Register #(.width(1), .Select("low")) register_2 (
    .D(or_2_out), .en(F_IIN), .Q(CF), .clk(BUS[16]), .clr(or_1_out), .cs(pull_resistor_7_node),
    .preset(pull_resistor_7_node));
  Multiplexer #(.width(16), .enable("false")) multiplexer_1 (
    .in0(adder_1_out), .in1(subtractor_1_out), .out(LEDS), .sel(SU));
  Pull_Resistor pull_resistor_8 (.node(LEDS));
  assign BUS_2[15:0] = E_OUT ? LEDS : 16'bz;  // Controlled_Buffer controlled_buffer_1
  nor nor_1 (nor_1_out, LEDS[15], LEDS[14], LEDS[13], LEDS[12], LEDS[11], LEDS[10], LEDS[9], LEDS[8], LEDS[7], LEDS[6], LEDS[5], LEDS[4], LEDS[3], LEDS[2], LEDS[1], LEDS[0]);
endmodule

module OUTPUT_7SEGMENT (
  input  [17:0] BUS,
  input  O_IN,
  input  O_RST,
  input  TWOS,
  input  _7S_CLK,
  output [7:0] _7SEG_0_7,
  output [7:0] _7SEG_8_15,
  output NEG,
  output LE_0,
  output LE_1
);

  wire and_2_out, or_1_out, pull_resistor_4_node, pull_resistor_5_node, pull_resistor_6_node;
  wire [15:0] register_1_q;

  Pull_Resistor pull_resistor_1 (.node(O_IN));
  Pull_Resistor pull_resistor_2 (.node(O_RST));
  Pull_Resistor pull_resistor_3 (.node(TWOS));
  and and_1 (NEG, BUS[15], TWOS);
  or or_1 (or_1_out, BUS[17], and_2_out);
  and and_2 (and_2_out, BUS[16], O_RST);
  Pull_Resistor pull_resistor_4 (.node(pull_resistor_4_node));
  Register #(.width(16), .Select("low")) register_1 (
    .D(BUS[15:0]), .en(O_IN), .Q(register_1_q), .clk(BUS[16]), .clr(or_1_out), .cs(pull_resistor_4_node),
    .preset(pull_resistor_4_node));
  Pull_Resistor pull_resistor_5 (.node(pull_resistor_5_node));
  Pull_Resistor pull_resistor_6 (.node(pull_resistor_6_node));
  ROM #(.addrWidth(13), .Select("low")) rom_1 (
    .addr({_7S_CLK, TWOS, 3'b000, register_1_q[7:0]}), .data(_7SEG_8_15), .sel(pull_resistor_5_node));
  ROM #(.addrWidth(13), .Select("low")) rom_2 (
    .addr({_7S_CLK, TWOS, 3'b000, register_1_q[15:8]}), .data(_7SEG_0_7), .sel(pull_resistor_6_node));
  Demultiplexer #(.enable("false")) demultiplexer_1 (.out0(LE_0), .out1(LE_1), .in(1'b1), .sel(_7S_CLK));

  // Notes on the sheet:
  //   NEG
  //   contents of rom_1 (hex, n*v repeats v):
  //   3f 6 5b 4f 66 6d 7d 7 7f 6f 77 7c 39 5e 79 71 3f 6 5b 4f 66 6d 7d 7 7f 6f 77 7c 39 5e 79 71 3f 6 5b
  //   4f 66 6d 7d 7 7f 6f 77 7c 39 5e 79 71 3f 6 5b 4f 66 6d 7d 7 7f 6f 77 7c 39 5e 79 71 3f 6 5b 4f 66 6d
  //   7d 7 7f 6f 77 7c 39 5e 79 71 3f 6 5b 4f 66 6d 7d 7 7f 6f 77 7c 39 5e 79 71 3f 6 5b 4f 66 6d 7d 7 7f
  //   6f 77 7c 39 5e 79 71 3f 6 5b 4f 66 6d 7d 7 7f 6f 77 7c 39 5e 79 71 3f 6 5b 4f 66 6d 7d 7 7f 6f 77 7c
  //   39 5e 79 71 3f 6 5b 4f 66 6d 7d 7 7f 6f 77 7c 39 5e 79 71 3f 6 5b 4f 66 6d 7d 7 7f 6f 77 7c 39 5e 79
  //   71 3f 6 5b 4f 66 6d 7d 7 7f 6f 77 7c 39 5e 79 71 3f 6 5b 4f 66 6d 7d 7 7f 6f 77 7c 39 5e 79 71 3f 6
  //   5b 4f 66 6d 7d 7 7f 6f 77 7c 39 5e 79 71 3f 6 5b 4f 66 6d 7d 7 7f 6f 77 7c 39 5e 79 71 3f 6 5b 4f 66
  //   6d 7d 7 7f 6f 77 7c 39 5e 79 71 3f 6 5b 4f 66 6d 7d 7 7f 6f 77 7c 39 5e 79 71 3f 6 5b 4f 66 6d 7d 7
  //   7f 6f 77 7c 39 5e 79 71 3f 6 5b 4f 66 6d 7d 7 7f 6f 77 7c 39 5e 79 71 3f 6 5b 4f 66 6d 7d 7 7f 6f 77
  //   7c 39 5e 79 71 3f 6 5b 4f 66 6d 7d 7 7f 6f 77 7c 39 5e 79 71 3f 6 5b 4f 66 6d 7d 7 7f 6f 77 7c 39 5e
  //   79 71 3f 6 5b 4f 66 6d 7d 7 7f 6f 77 7c 39 5e 79 71 3f 6 5b 4f 66 6d 7d 7 7f 6f 77 7c 39 5e 79 71 3f
  //   6 5b 4f 66 6d 7d 7 7f 6f 77 7c 39 5e 79 71 3f 6 5b 4f 66 6d 7d 7 7f 6f 77 7c 39 5e 79 71 3f 6 5b 4f
  //   66 6d 7d 7 7f 6f 77 7c 39 5e 79 71 3f 6 5b 4f 66 6d 7d 7 7f 6f 77 7c 39 5e 79 71 3f 6 5b 4f 66 6d 7d
  //   7 7f 6f 77 7c 39 5e 79 71 3f 6 5b 4f 66 6d 7d 7 7f 6f 77 7c 39 5e 79 71 3f 6 5b 4f 66 6d 7d 7 7f 6f
  //   77 7c 39 5e 79 71 3f 6 5b 4f 66 6d 7d 7 7f 6f 77 7c 39 5e 79 71 3f 6 5b 4f 66 6d 7d 7 7f 6f 77 7c 39
  //   5e 79 71 3f 6 5b 4f 66 6d 7d 7 7f 6f 77 7c 39 5e 79 71 3f 6 5b 4f 66 6d 7d 7 7f 6f 77 7c 39 5e 79 71
  //   3f 6 5b 4f 66 6d 7d 7 7f 6f 77 7c 39 5e 79 71 3f 6 5b 4f 66 6d 7d 7 7f 6f 77 7c 39 5e 79 71 3f 6 5b
  //   4f 66 6d 7d 7 7f 6f 77 7c 39 5e 79 71 3f 6 5b 4f 66 6d 7d 7 7f 6f 77 7c 39 5e 79 71 3f 6 5b 4f 66 6d
  //   7d 7 7f 6f 77 7c 39 5e 79 71 3f 6 5b 4f 66 6d 7d 7 7f 6f 77 7c 39 5e 79 71 3f 6 5b 4f 66 6d 7d 7 7f
  //   6f 77 7c 39 5e 79 71 3f 6 5b 4f 66 6d 7d 7 7f 6f 77 7c 39 5e 79 71 3f 6 5b 4f 66 6d 7d 7 7f 6f 77 7c
  //   39 5e 79 71 3f 6 5b 4f 66 6d 7d 7 7f 6f 77 7c 39 5e 79 71 3f 6 5b 4f 66 6d 7d 7 7f 6f 77 7c 39 5e 79
  //   71 3f 6 5b 4f 66 6d 7d 7 7f 6f 77 7c 39 5e 79 71 3f 6 5b 4f 66 6d 7d 7 7f 6f 77 7c 39 5e 79 71 3f 6
  //   5b 4f 66 6d 7d 7 7f 6f 77 7c 39 5e 79 71 3f 6 5b 4f 66 6d 7d 7 7f 6f 77 7c 39 5e 79 71 3f 6 5b 4f 66
  //   6d 7d 7 7f 6f 77 7c 39 5e 79 71 3f 6 5b 4f 66 6d 7d 7 7f 6f 77 7c 39 5e 79 71 3f 6 5b 4f 66 6d 7d 7
  //   7f 6f 77 7c 39 5e 79 71 3f 6 5b 4f 66 6d 7d 7 7f 6f 77 7c 39 5e 79 71 3f 6 5b 4f 66 6d 7d 7 7f 6f 77
  //   7c 39 5e 79 71 3f 6 5b 4f 66 6d 7d 7 7f 6f 77 7c 39 5e 79 71 3f 6 5b 4f 66 6d 7d 7 7f 6f 77 7c 39 5e
  //   79 71 3f 6 5b 4f 66 6d 7d 7 7f 6f 77 7c 39 5e 79 71 3f 6 5b 4f 66 6d 7d 7 7f 6f 77 7c 39 5e 79 71 3f
  //   6 5b 4f 66 6d 7d 7 7f 6f 77 7c 39 5e 79 71 3f 6 5b 4f 66 6d 7d 7 7f 6f 77 7c 39 5e 79 71 3f 6 5b 4f
  //   66 6d 7d 7 7f 6f 77 7c 39 5e 79 71 3f 6 5b 4f 66 6d 7d 7 7f 6f 77 7c 39 5e 79 71 3f 6 5b 4f 66 6d 7d
  //   7 7f 6f 77 7c 39 5e 79 71 3f 6 5b 4f 66 6d 7d 7 7f 6f 77 7c 39 5e 79 71 3f 6 5b 4f 66 6d 7d 7 7f 6f
  //   77 7c 39 5e 79 71 3f 6 5b 4f 66 6d 7d 7 7f 6f 77 7c 39 5e 79 71 3f 6 5b 4f 66 6d 7d 7 7f 6f 77 7c 39
  //   5e 79 71 3f 6 5b 4f 66 6d 7d 7 7f 6f 77 7c 39 5e 79 71 3f 6 5b 4f 66 6d 7d 7 7f 6f 77 7c 39 5e 79 71
  //   3f 6 5b 4f 66 6d 7d 7 7f 6f 77 7c 39 5e 79 71 3f 6 5b 4f 66 6d 7d 7 7f 6f 77 7c 39 5e 79 71 3f 6 5b
  //   4f 66 6d 7d 7 7f 6f 77 7c 39 5e 79 71 3f 6 5b 4f 66 6d 7d 7 7f 6f 77 7c 39 5e 79 71 3f 6 5b 4f 66 6d
  //   7d 7 7f 6f 77 7c 39 5e 79 71 3f 6 5b 4f 66 6d 7d 7 7f 6f 77 7c 39 5e 79 71 3f 6 5b 4f 66 6d 7d 7 7f
  //   6f 77 7c 39 5e 79 71 3f 6 5b 4f 66 6d 7d 7 7f 6f 77 7c 39 5e 79 71 3f 6 5b 4f 66 6d 7d 7 7f 6f 77 7c
  //   39 5e 79 71 3f 6 5b 4f 66 6d 7d 7 7f 6f 77 7c 39 5e 79 71 3f 6 5b 4f 66 6d 7d 7 7f 6f 77 7c 39 5e 79
  //   71 3f 6 5b 4f 66 6d 7d 7 7f 6f 77 7c 39 5e 79 71 3f 6 5b 4f 66 6d 7d 7 7f 6f 77 7c 39 5e 79 71 3f 6
  //   5b 4f 66 6d 7d 7 7f 6f 77 7c 39 5e 79 71 3f 6 5b 4f 66 6d 7d 7 7f 6f 77 7c 39 5e 79 71 3f 6 5b 4f 66
  //   6d 7d 7 7f 6f 77 7c 39 5e 79 71 3f 6 5b 4f 66 6d 7d 7 7f 6f 77 7c 39 5e 79 7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
  //   contents of rom_2 (hex, n*v repeats v):
  //   3f 6 5b 4f 66 6d 7d 7 7f 6f 77 7c 39 5e 79 71 3f 6 5b 4f 66 6d 7d 7 7f 6f 77 7c 39 5e 79 71 3f 6 5b
  //   4f 66 6d 7d 7 7f 6f 77 7c 39 5e 79 71 3f 6 5b 4f 66 6d 7d 7 7f 6f 77 7c 39 5e 79 71 3f 6 5b 4f 66 6d
  //   7d 7 7f 6f 77 7c 39 5e 79 71 3f 6 5b 4f 66 6d 7d 7 7f 6f 77 7c 39 5e 79 71 3f 6 5b 4f 66 6d 7d 7 7f
  //   6f 77 7c 39 5e 79 71 3f 6 5b 4f 66 6d 7d 7 7f 6f 77 7c 39 5e 79 71 3f 6 5b 4f 66 6d 7d 7 7f 6f 77 7c
  //   39 5e 79 71 3f 6 5b 4f 66 6d 7d 7 7f 6f 77 7c 39 5e 79 71 3f 6 5b 4f 66 6d 7d 7 7f 6f 77 7c 39 5e 79
  //   71 3f 6 5b 4f 66 6d 7d 7 7f 6f 77 7c 39 5e 79 71 3f 6 5b 4f 66 6d 7d 7 7f 6f 77 7c 39 5e 79 71 3f 6
  //   5b 4f 66 6d 7d 7 7f 6f 77 7c 39 5e 79 71 3f 6 5b 4f 66 6d 7d 7 7f 6f 77 7c 39 5e 79 71 3f 6 5b 4f 66
  //   6d 7d 7 7f 6f 77 7c 39 5e 79 71 3f 6 5b 4f 66 6d 7d 7 7f 6f 77 7c 39 5e 79 71 3f 6 5b 4f 66 6d 7d 7
  //   7f 6f 77 7c 39 5e 79 71 3f 6 5b 4f 66 6d 7d 7 7f 6f 77 7c 39 5e 79 71 3f 6 5b 4f 66 6d 7d 7 7f 6f 77
  //   7c 39 5e 79 71 3f 6 5b 4f 66 6d 7d 7 7f 6f 77 7c 39 5e 79 71 3f 6 5b 4f 66 6d 7d 7 7f 6f 77 7c 39 5e
  //   79 71 3f 6 5b 4f 66 6d 7d 7 7f 6f 77 7c 39 5e 79 71 3f 6 5b 4f 66 6d 7d 7 7f 6f 77 7c 39 5e 79 71 3f
  //   6 5b 4f 66 6d 7d 7 7f 6f 77 7c 39 5e 79 71 3f 6 5b 4f 66 6d 7d 7 7f 6f 77 7c 39 5e 79 71 3f 6 5b 4f
  //   66 6d 7d 7 7f 6f 77 7c 39 5e 79 71 3f 6 5b 4f 66 6d 7d 7 7f 6f 77 7c 39 5e 79 71 3f 6 5b 4f 66 6d 7d
  //   7 7f 6f 77 7c 39 5e 79 71 3f 6 5b 4f 66 6d 7d 7 7f 6f 77 7c 39 5e 79 71 3f 6 5b 4f 66 6d 7d 7 7f 6f
  //   77 7c 39 5e 79 71 3f 6 5b 4f 66 6d 7d 7 7f 6f 77 7c 39 5e 79 71 3f 6 5b 4f 66 6d 7d 7 7f 6f 77 7c 39
  //   5e 79 71 3f 6 5b 4f 66 6d 7d 7 7f 6f 77 7c 39 5e 79 71 3f 6 5b 4f 66 6d 7d 7 7f 6f 77 7c 39 5e 79 71
  //   3f 6 5b 4f 66 6d 7d 7 7f 6f 77 7c 39 5e 79 71 3f 6 5b 4f 66 6d 7d 7 7f 6f 77 7c 39 5e 79 71 3f 6 5b
  //   4f 66 6d 7d 7 7f 6f 77 7c 39 5e 79 71 3f 6 5b 4f 66 6d 7d 7 7f 6f 77 7c 39 5e 79 71 3f 6 5b 4f 66 6d
  //   7d 7 7f 6f 77 7c 39 5e 79 71 3f 6 5b 4f 66 6d 7d 7 7f 6f 77 7c 39 5e 79 71 3f 6 5b 4f 66 6d 7d 7 7f
  //   6f 77 7c 39 5e 79 71 3f 6 5b 4f 66 6d 7d 7 7f 6f 77 7c 39 5e 79 71 3f 6 5b 4f 66 6d 7d 7 7f 6f 77 7c
  //   39 5e 79 71 3f 6 5b 4f 66 6d 7d 7 7f 6f 77 7c 39 5e 79 71 3f 6 5b 4f 66 6d 7d 7 7f 6f 77 7c 39 5e 79
  //   71 3f 6 5b 4f 66 6d 7d 7 7f 6f 77 7c 39 5e 79 71 3f 6 5b 4f 66 6d 7d 7 7f 6f 77 7c 39 5e 79 71 3f 6
  //   5b 4f 66 6d 7d 7 7f 6f 77 7c 39 5e 79 71 3f 6 5b 4f 66 6d 7d 7 7f 6f 77 7c 39 5e 79 71 3f 6 5b 4f 66
  //   6d 7d 7 7f 6f 77 7c 39 5e 79 71 3f 6 5b 4f 66 6d 7d 7 7f 6f 77 7c 39 5e 79 71 3f 6 5b 4f 66 6d 7d 7
  //   7f 6f 77 7c 39 5e 79 71 3f 6 5b 4f 66 6d 7d 7 7f 6f 77 7c 39 5e 79 71 3f 6 5b 4f 66 6d 7d 7 7f 6f 77
  //   7c 39 5e 79 71 3f 6 5b 4f 66 6d 7d 7 7f 6f 77 7c 39 5e 79 71 3f 6 5b 4f 66 6d 7d 7 7f 6f 77 7c 39 5e
  //   79 71 3f 6 5b 4f 66 6d 7d 7 7f 6f 77 7c 39 5e 79 71 3f 6 5b 4f 66 6d 7d 7 7f 6f 77 7c 39 5e 79 71 3f
  //   6 5b 4f 66 6d 7d 7 7f 6f 77 7c 39 5e 79 71 3f 6 5b 4f 66 6d 7d 7 7f 6f 77 7c 39 5e 79 71 3f 6 5b 4f
  //   66 6d 7d 7 7f 6f 77 7c 39 5e 79 71 3f 6 5b 4f 66 6d 7d 7 7f 6f 77 7c 39 5e 79 71 3f 6 5b 4f 66 6d 7d
  //   7 7f 6f 77 7c 39 5e 79 71 3f 6 5b 4f 66 6d 7d 7 7f 6f 77 7c 39 5e 79 71 3f 6 5b 4f 66 6d 7d 7 7f 6f
  //   77 7c 39 5e 79 71 3f 6 5b 4f 66 6d 7d 7 7f 6f 77 7c 39 5e 79 71 3f 6 5b 4f 66 6d 7d 7 7f 6f 77 7c 39
  //   5e 79 71 3f 6 5b 4f 66 6d 7d 7 7f 6f 77 7c 39 5e 79 71 3f 6 5b 4f 66 6d 7d 7 7f 6f 77 7c 39 5e 79 71
  //   3f 6 5b 4f 66 6d 7d 7 7f 6f 77 7c 39 5e 79 71 3f 6 5b 4f 66 6d 7d 7 7f 6f 77 7c 39 5e 79 71 3f 6 5b
  //   4f 66 6d 7d 7 7f 6f 77 7c 39 5e 79 71 3f 6 5b 4f 66 6d 7d 7 7f 6f 77 7c 39 5e 79 71 3f 6 5b 4f 66 6d
  //   7d 7 7f 6f 77 7c 39 5e 79 71 3f 6 5b 4f 66 6d 7d 7 7f 6f 77 7c 39 5e 79 71 3f 6 5b 4f 66 6d 7d 7 7f
  //   6f 77 7c 39 5e 79 71 3f 6 5b 4f 66 6d 7d 7 7f 6f 77 7c 39 5e 79 71 3f 6 5b 4f 66 6d 7d 7 7f 6f 77 7c
  //   39 5e 79 71 3f 6 5b 4f 66 6d 7d 7 7f 6f 77 7c 39 5e 79 71 3f 6 5b 4f 66 6d 7d 7 7f 6f 77 7c 39 5e 79
  //   71 3f 6 5b 4f 66 6d 7d 7 7f 6f 77 7c 39 5e 79 71 3f 6 5b 4f 66 6d 7d 7 7f 6f 77 7c 39 5e 79 71 3f 6
  //   5b 4f 66 6d 7d 7 7f 6f 77 7c 39 5e 79 71 3f 6 5b 4f 66 6d 7d 7 7f 6f 77 7c 39 5e 79 71 3f 6 5b 4f 66
  //   6d 7d 7 7f 6f 77 7c 39 5e 79 71 3f 6 5b 4f 66 6d 7d 7 7f 6f 77 7c 39 5e 79 7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
  //   7S_CLK
endmodule

module RAM_ADDR_REGISTER (
  input  [17:0] BUS,
  input  MA_IN,
  input  MA_RST,
  output [15:0] RAM_BUS
);

  wire and_1_out, or_1_out, pull_resistor_1_node;

  or or_1 (or_1_out, BUS[17], and_1_out);
  and and_1 (and_1_out, BUS[16], MA_RST);
  Pull_Resistor pull_resistor_1 (.node(pull_resistor_1_node));
  Register #(.width(16), .Select("low")) register_1 (
    .D(BUS[15:0]), .en(MA_IN), .Q(RAM_BUS), .clk(BUS[16]), .clr(or_1_out), .cs(pull_resistor_1_node),
    .preset(pull_resistor_1_node));
endmodule

module RAM (
  input  [17:0] BUS,
  input  [15:0] RAM_BUS,
  input  M_IN,
  input  M_OUT,
  input  COPY_CLK,
  output [17:0] BUS_2
);

  wire and_1_out, not_1_out, pull_resistor_1_node, pull_resistor_3_node;
  wire [15:0] controlled_buffer_1_out;

  Pull_Resistor pull_resistor_1 (.node(pull_resistor_1_node));
  buf buffer_1 (pull_resistor_1_node, BUS[16]);
  Pull_Resistor pull_resistor_2 (.node(M_IN));
  buf buffer_2 (pull_resistor_1_node, COPY_CLK);
  and and_1 (and_1_out, pull_resistor_1_node, M_IN);
  Pull_Resistor pull_resistor_3 (.node(pull_resistor_3_node));
  Pull_Resistor pull_resistor_4 (.node(M_OUT));
  not not_1 (not_1_out, M_OUT);
  assign controlled_buffer_1_out = not_1_out ? BUS[15:0] : 16'bz;  // Controlled_Buffer controlled_buffer_1
  RAM_part #(.addrWidth(16), .dataWidth(16), .Select("low")) ram_1 (
    .addr(RAM_BUS), .data(controlled_buffer_1_out), .sel(pull_resistor_3_node), .clk(and_1_out), .ld(M_OUT));  // open: clr
  assign BUS_2[15:0] = M_OUT ? controlled_buffer_1_out : 16'bz;  // Controlled_Buffer controlled_buffer_2

  // Notes on the sheet:
  //   buffer_1 drives only 1 and floats otherwise
  //   buffer_2 drives only 1 and floats otherwise
endmodule

module CONTROL_LOGIC (
  input  [17:0] BUS,
  input  ZF,
  input  CF,
  input  CLC_RST,
  input  [7:0] I_BUS,
  input  AUTO,
  output [3:0] STEP,
  output [31:0] CLO
);

  wire not_1_out, or_1_out, pull_resistor_3_node;
  wire [31:0] rom_1_data;

  Pull_Resistor pull_resistor_1 (.node(CLC_RST));
  // AND_Gate and_1 has open pins: in0=BUS[16], out=open
  Pull_Resistor pull_resistor_2 (.node(AUTO));
  not not_1 (not_1_out, BUS[16]);
  or or_1 (or_1_out, BUS[17], CLC_RST);
  Pull_Resistor pull_resistor_3 (.node(pull_resistor_3_node));
  Counter #(.width(4), .max('hf)) counter_1 (
    .load(1'b0), .count(1'b1), .Q(STEP), .clk(not_1_out), .clr(or_1_out), .preset(1'b0), .down(1'b0));  // open: D, carry
  ROM #(.addrWidth(14), .dataWidth(32), .Select("low")) rom_1 (
    .addr({I_BUS, STEP, CF, ZF}), .data(rom_1_data), .sel(pull_resistor_3_node));
  assign CLO = AUTO ? rom_1_data : 32'bz;  // Controlled_Buffer controlled_buffer_1

  // Notes on the sheet:
  //   contents of rom_1 (hex, n*v repeats v):
  //   4*80008000 4*40001800 4*100 52*0 4*80008000 4*40001800 4*11000000 4*100 48*0 4*80008000 4*40001800
  //   4*10000400 4*100 48*0 4*80008000 4*40001800 4*4000 4*8400 4*10001000 4*100 40*0 4*80008000
  //   4*40001800 4*8008000 4*1002000 4*100 44*0 4*80008000 4*40001800 4*8008000 4*8400 4*100 44*0
  //   4*80008000 4*40001800 4*100 52*0 4*80008000 4*40001800 4*a000000 4*100 48*0 4*80008000 4*40001800
  //   4*2000400 4*100 48*0 4*80008000 4*40001800 4*4000 4*8400 4*2001000 4*100 40*0 4*80008000 4*40001800
  //   4*1008000 4*8002000 4*100 44*0 4*80008000 4*40001800 4*1008000 4*8400 4*100 44*0 4*80008000
  //   4*40001800 4*100 52*0 4*80008000 4*40001800 4*4000 4*8400 4*8002000 4*100 40*0 4*80008000 4*40001800
  //   4*4000 4*8400 4*1002000 4*100 40*0 4*80008000 4*40001800 4*100 52*0 4*80008000 4*40001800 4*100 52*0
  //   4*80008000 4*40001800 4*200000 4*10180000 4*100 44*0 4*80008000 4*40001800 4*2200400 4*10180000
  //   4*100 44*0 4*80008000 4*40001800 4*204000 4*8400 4*2001000 4*10180000 4*100 36*0 4*80008000
  //   4*40001800 4*200000 4*10580000 4*100 44*0 4*80008000 4*40001800 4*2200400 4*10580000 4*100 44*0
  //   4*80008000 4*40001800 4*204000 4*8400 4*2001000 4*10580000 4*100 36*0 4*80008000 4*40001800
  //   4*60200400 4*100 48*0 4*80008000 4*40001800 40200000 60200400 40200000 60200400 4*100 48*0
  //   4*80008000 4*40001800 40200000 40200000 60200400 60200400 4*100 48*0 4*80008000 4*40001800 4*200000
  //   4*100000 4*100 44*0 4*80008000 4*40001800 4*200000 4*2000400 4*100000 4*100 40*0 4*80008000
  //   4*40001800 4*100 52*0 4*80008000 4*40001800 4*100 52*0 4*80008000 4*40001800 200000 200000 20200400
  //   20200400 4*100 48*0 4*80008000 4*40001800 100 20200400 20200400 20200400 0 100 100 100 48*0
  //   4*80008000 4*40001800 100 20200400 100 20200400 0 100 0 100 48*0 4*80008000 4*40001800 20200400
  //   20200400 100 20200400 100 100 0 100 48*0 4*80008000 4*40001800 20200400 4*100 51*0 4*80008000
  //   4*40001800 4*100 52*0 4*80008000 4*40001800 4*8040000 4*100 48*0 4*80008000 4*40001800 4*1040000
  //   4*100 48*0 4*80008000 4*40001800 4*40400 4*100 48*0 4*80008000 4*40001800 4*4000 4*8400 4*41000
  //   4*100 40*0 4*80008000 4*40001800 4*100 52*0 4*80008000 4*40001800 4*100 52*0 4*80008000 4*40001800
  //   4*100 52*0 4*80008000 4*40001800 4*100 52*0 4*80008000 4*40001800 4*100 52*0 4*80008000 4*40001800
  //   4*100 52*0 4*80008000 4*40001800 4*100 52*0 4*80008000 4*40001800 4*100 52*0 4*80008000 4*40001800
  //   4*100 52*0 4*80008000 4*40001800 4*100 52*0 4*80008000 4*40001800 4*100 52*0 4*80008000 4*40001800
  //   4*100 52*0 4*80008000 4*40001800 4*100 52*0 4*80008000 4*40001800 4*100 52*0 4*80008000 4*40001800
  //   4*100 52*0 4*80008000 4*40001800 4*100 52*0 4*80008000 4*40001800 4*100 52*0 4*80008000 4*40001800
  //   4*100 52*0 4*80008000 4*40001800 4*100 52*0 4*80008000 4*40001800 4*100 52*0 4*80008000 4*40001800
  //   4*100 52*0 4*80008000 4*40001800 4*100 52*0 4*80008000 4*40001800 4*100 52*0 4*80008000 4*40001800
  //   4*100 52*0 4*80008000 4*40001800 4*100 52*0 4*80008000 4*40001800 4*100 52*0 4*80008000 4*40001800
  //   4*100 52*0 4*80008000 4*40001800 4*100 52*0 4*80008000 4*40001800 4*100 52*0 4*80008000 4*40001800
  //   4*100 52*0 4*80008000 4*40001800 4*100 52*0 4*80008000 4*40001800 4*100 52*0 4*80008000 4*40001800
  //   4*100 52*0 4*80008000 4*40001800 4*100 52*0 4*80008000 4*40001800 4*100 52*0 4*80008000 4*40001800
  //   4*100 52*0 4*80008000 4*40001800 4*100 52*0 4*80008000 4*40001800 4*100 52*0 4*80008000 4*40001800
  //   4*100 52*0 4*80008000 4*40001800 4*100 52*0 4*80008000 4*40001800 4*100 52*0 4*80008000 4*40001800
  //   4*100 52*0 4*80008000 4*40001800 4*100 52*0 4*80008000 4*40001800 4*100 52*0 4*80008000 4*40001800
  //   4*100 52*0 4*80008000 4*40001800 4*100 52*0 4*80008000 4*40001800 4*100 52*0 4*80008000 4*40001800
  //   4*100 52*0 4*80008000 4*40001800 4*100 52*0 4*80008000 4*40001800 4*100 52*0 4*80008000 4*40001800
  //   4*100 52*0 4*80008000 4*40001800 4*100 52*0 4*80008000 4*40001800 4*100 52*0 4*80008000 4*40001800
  //   4*100 52*0 4*80008000 4*40001800 4*100 52*0 4*80008000 4*40001800 4*100 52*0 4*80008000 4*40001800
  //   4*100 52*0 4*80008000 4*40001800 4*100 52*0 4*80008000 4*40001800 4*100 52*0 4*80008000 4*40001800
  //   4*100 52*0 4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
endmodule

module PROGRAM_ROM (
  input  ENB,
  input  R_CLK,
  input  R_RST,
  output DONE,
  output [15:0] ADDR,
  output [15:0] DATA
);

  wire and_1_out, and_2_out, buffer_1_out, counter_1_carry, not_1_out, pull_resistor_1_node;

  not not_1 (not_1_out, DONE);
  and and_1 (and_1_out, not_1_out, R_CLK);
  Pull_Resistor pull_resistor_1 (.node(pull_resistor_1_node));
  Counter #(.width(16), .max('hffff)) counter_1 (
    .load(1'b0), .count(ENB), .Q(ADDR), .carry(counter_1_carry), .clk(and_1_out), .clr(R_RST), .preset(1'b0),
    .down(1'b0));  // open: D
  ROM #(.addrWidth(16), .dataWidth(16), .Select("low")) rom_1 (.addr(ADDR), .data(DATA), .sel(pull_resistor_1_node));
  buf buffer_1 (buffer_1_out, counter_1_carry);
  and and_2 (and_2_out, R_CLK, buffer_1_out);
  D_Flip_Flop d_ff_1 (.clk(and_2_out), .D(buffer_1_out), .Q(DONE), .preset(1'b0), .reset(R_RST));  // open: Qn
  and and_3 (buffer_1_out, DATA[0], DATA[1], DATA[2], DATA[3], DATA[4], DATA[5], DATA[6], DATA[7], DATA[8], DATA[9], DATA[10], DATA[11], DATA[12], DATA[13], DATA[14], DATA[15]);

  // Notes on the sheet:
  //   contents of rom_1 (hex, n*v repeats v):
  //   200 801 2400 1100 2400 1703 ff00 ffff
  //   buffer_1 drives only 1 and floats otherwise
endmodule

module PLEX_16 (
  input  [15:0] B16_1,
  input  [15:0] B16_2,
  input  B16_SEL,
  output [15:0] B16_3
);

  Multiplexer #(.width(16), .enable("false")) multiplexer_1 (.in0(B16_1), .in1(B16_2), .out(B16_3), .sel(B16_SEL));
endmodule

module PLEX_18 (
  input  [17:0] B18_1,
  input  [17:0] B18_2,
  input  B18_SEL,
  output [17:0] B18_3
);

  Multiplexer #(.width(18), .enable("false")) multiplexer_1 (.in0(B18_1), .in1(B18_2), .out(B18_3), .sel(B18_SEL));
endmodule

module GEN_REGISTER (
  input  [17:0] BUS,
  input  IN,
  input  OUT,
  input  RST,
  output [17:0] BUS_2,
  output [15:0] LEDS,
  output [15:0] A_BUS
);

  wire and_1_out, or_1_out, pull_resistor_2_node;

  or or_1 (or_1_out, BUS[17], and_1_out);
  and and_1 (and_1_out, BUS[16], RST);
  Pull_Resistor pull_resistor_1 (.node(OUT));
  Pull_Resistor pull_resistor_2 (.node(pull_resistor_2_node));
  Register #(.width(16), .Select("low")) register_1 (
    .D(BUS[15:0]), .en(IN), .Q(A_BUS), .clk(BUS[16]), .clr(or_1_out), .cs(pull_resistor_2_node),
    .preset(pull_resistor_2_node));
  Pull_Resistor pull_resistor_3 (.node(or_1_out));
  Pull_Resistor pull_resistor_4 (.node(IN));
  Pull_Resistor pull_resistor_5 (.node(A_BUS));
  assign BUS_2[15:0] = OUT ? A_BUS : 16'bz;  // Controlled_Buffer controlled_buffer_1

  assign LEDS = A_BUS;
endmodule

module _7SEG_DMX (
  input  [7:0] _7SEG_0_7,
  input  [7:0] _7SEG_8_15,
  input  LE,
  output [7:0] _7SEG_0_7_0,
  output [7:0] _7SEG_0_7_1,
  output [7:0] _7SEG_8_15_0,
  output [7:0] _7SEG_8_15_1
);

  Demultiplexer #(.width(8), .enable("false")) demultiplexer_1 (
    .out0(_7SEG_0_7_0), .out1(_7SEG_0_7_1), .in(_7SEG_0_7), .sel(LE));
  Pull_Resistor pull_resistor_1 (.node(_7SEG_0_7_0[0]));
  Pull_Resistor pull_resistor_2 (.node(_7SEG_0_7_0[1]));
  Pull_Resistor pull_resistor_3 (.node(_7SEG_0_7_0[2]));
  Pull_Resistor pull_resistor_4 (.node(_7SEG_0_7_0[3]));
  Pull_Resistor pull_resistor_5 (.node(_7SEG_0_7_0[4]));
  Pull_Resistor pull_resistor_6 (.node(_7SEG_0_7_0[5]));
  Pull_Resistor pull_resistor_7 (.node(_7SEG_0_7_0[6]));
  Pull_Resistor pull_resistor_8 (.node(_7SEG_0_7_0[7]));
  Pull_Resistor pull_resistor_9 (.node(_7SEG_0_7_1[0]));
  Pull_Resistor pull_resistor_10 (.node(_7SEG_0_7_1[1]));
  Pull_Resistor pull_resistor_11 (.node(_7SEG_0_7_1[2]));
  Pull_Resistor pull_resistor_12 (.node(_7SEG_0_7_1[3]));
  Pull_Resistor pull_resistor_13 (.node(_7SEG_0_7_1[4]));
  Pull_Resistor pull_resistor_14 (.node(_7SEG_0_7_1[5]));
  Pull_Resistor pull_resistor_15 (.node(_7SEG_0_7_1[6]));
  Pull_Resistor pull_resistor_16 (.node(_7SEG_0_7_1[7]));
  Demultiplexer #(.width(8), .enable("false")) demultiplexer_2 (
    .out0(_7SEG_8_15_0), .out1(_7SEG_8_15_1), .in(_7SEG_8_15), .sel(LE));
  Pull_Resistor pull_resistor_17 (.node(_7SEG_8_15_0[0]));
  Pull_Resistor pull_resistor_18 (.node(_7SEG_8_15_0[1]));
  Pull_Resistor pull_resistor_19 (.node(_7SEG_8_15_0[2]));
  Pull_Resistor pull_resistor_20 (.node(_7SEG_8_15_0[3]));
  Pull_Resistor pull_resistor_21 (.node(_7SEG_8_15_0[4]));
  Pull_Resistor pull_resistor_22 (.node(_7SEG_8_15_0[5]));
  Pull_Resistor pull_resistor_23 (.node(_7SEG_8_15_0[6]));
  Pull_Resistor pull_resistor_24 (.node(_7SEG_8_15_0[7]));
  Pull_Resistor pull_resistor_25 (.node(_7SEG_8_15_1[0]));
  Pull_Resistor pull_resistor_26 (.node(_7SEG_8_15_1[1]));
  Pull_Resistor pull_resistor_27 (.node(_7SEG_8_15_1[2]));
  Pull_Resistor pull_resistor_28 (.node(_7SEG_8_15_1[3]));
  Pull_Resistor pull_resistor_29 (.node(_7SEG_8_15_1[4]));
  Pull_Resistor pull_resistor_30 (.node(_7SEG_8_15_1[5]));
  Pull_Resistor pull_resistor_31 (.node(_7SEG_8_15_1[6]));
  Pull_Resistor pull_resistor_32 (.node(_7SEG_8_15_1[7]));
endmodule
